// Logisim project 3zad.circ as structural Verilog: 2 circuits, main circuit 1bit
module _1bit (
  input  in_1,
  input  in_2,
  input  in_3,
  input  in_4,
  input  in_5,
  output out,
  output out_2,
  output out_3
);

  wire nor_1_out, nor_2_out, nor_3_out, nor_4_out, nor_5_out, nor_6_out, nor_7_out, nor_8_out, nor_10_out,
       nor_11_out, not_1_out, not_2_out, not_3_out, not_4_out, not_5_out, not_6_out, not_7_out, not_8_out;

  not not_1 (not_1_out, in_2);
  not not_2 (not_2_out, in_1);
  nor nor_1 (nor_1_out, in_1, in_2);
  nor nor_2 (nor_2_out, in_1, not_1_out);
  nor nor_3 (nor_3_out, not_2_out, in_2);
  nor nor_4 (nor_4_out, in_1, nor_1_out);
  nor nor_5 (nor_5_out, nor_1_out, in_2);
  nor nor_6 (nor_6_out, nor_4_out, nor_5_out);
  not not_3 (not_3_out, nor_2_out);
  not not_4 (not_4_out, in_3);
  not not_5 (not_5_out, nor_3_out);
  not not_6 (not_6_out, in_3);
  not not_7 (not_7_out, nor_6_out);
  not not_8 (not_8_out, in_3);
  nor nor_7 (nor_7_out, not_3_out, not_4_out);
  nor nor_8 (nor_8_out, not_5_out, not_6_out);
  nor nor_9 (out_3, not_7_out, not_8_out);
  nor nor_10 (nor_10_out, nor_7_out, in_4);
  nor nor_11 (nor_11_out, nor_8_out, in_5);
  nor nor_12 (out, nor_10_out, nor_10_out);
  nor nor_13 (out_2, nor_11_out, nor_11_out);
endmodule

module _8bit (
  input  [7:0] in_1,
  input  [7:0] in_2,
  input  in_3,
  input  in_4,
  input  in_5,
  output out_6,
  output out_7,
  output out_8
);

  wire n1bit_1_out, n1bit_1_out_2, n1bit_1_out_3, n1bit_2_out, n1bit_2_out_2, n1bit_2_out_3, n1bit_3_out,
       n1bit_3_out_2, n1bit_3_out_3, n1bit_4_out, n1bit_4_out_2, n1bit_4_out_3, n1bit_5_out, n1bit_5_out_2,
       n1bit_5_out_3, n1bit_6_out, n1bit_6_out_2, n1bit_6_out_3, n1bit_7_out, n1bit_7_out_2, n1bit_7_out_3;

  _1bit u_1bit_1 (
    .in_1(in_1[7]), .in_2(in_2[7]), .in_3(in_3), .in_4(in_4), .in_5(in_5), .out(n1bit_1_out),
    .out_2(n1bit_1_out_2), .out_3(n1bit_1_out_3));
  _1bit u_1bit_2 (
    .in_1(in_1[6]), .in_2(in_2[6]), .in_3(n1bit_1_out_3), .in_4(n1bit_1_out), .in_5(n1bit_1_out_2),
    .out(n1bit_2_out), .out_2(n1bit_2_out_2), .out_3(n1bit_2_out_3));
  _1bit u_1bit_3 (
    .in_1(in_1[5]), .in_2(in_2[5]), .in_3(n1bit_2_out_3), .in_4(n1bit_2_out), .in_5(n1bit_2_out_2),
    .out(n1bit_3_out), .out_2(n1bit_3_out_2), .out_3(n1bit_3_out_3));
  _1bit u_1bit_4 (
    .in_1(in_1[4]), .in_2(in_2[4]), .in_3(n1bit_3_out_3), .in_4(n1bit_3_out), .in_5(n1bit_3_out_2),
    .out(n1bit_4_out), .out_2(n1bit_4_out_2), .out_3(n1bit_4_out_3));
  _1bit u_1bit_5 (
    .in_1(in_1[3]), .in_2(in_2[3]), .in_3(n1bit_4_out_3), .in_4(n1bit_4_out), .in_5(n1bit_4_out_2),
    .out(n1bit_5_out), .out_2(n1bit_5_out_2), .out_3(n1bit_5_out_3));
  _1bit u_1bit_6 (
    .in_1(in_1[2]), .in_2(in_2[2]), .in_3(n1bit_5_out_3), .in_4(n1bit_5_out), .in_5(n1bit_5_out_2),
    .out(n1bit_6_out), .out_2(n1bit_6_out_2), .out_3(n1bit_6_out_3));
  _1bit u_1bit_7 (
    .in_1(in_1[1]), .in_2(in_2[1]), .in_3(n1bit_6_out_3), .in_4(n1bit_6_out), .in_5(n1bit_6_out_2),
    .out(n1bit_7_out), .out_2(n1bit_7_out_2), .out_3(n1bit_7_out_3));
  _1bit u_1bit_8 (
    .in_1(in_1[0]), .in_2(in_2[0]), .in_3(n1bit_7_out_3), .in_4(n1bit_7_out), .in_5(n1bit_7_out_2),
    .out(out_6), .out_2(out_7), .out_3(out_8));
endmodule
