// Logisim project 4.circ as structural Verilog: 2 circuits, main circuit main
module main (
  input  X,
  input  Y,
  input  in_3,
  input  in_4,
  input  in_5,
  output x_y,
  output x_y_2,
  output x_y_3
);

  wire nor_1_out, nor_2_out, nor_3_out, not_1_out, not_2_out, not_3_out, not_4_out, not_5_out, not_6_out,
       not_7_out, not_8_out;

  not not_1 (not_1_out, Y);
  not not_2 (not_2_out, X);
  nor nor_1 (nor_1_out, X, not_1_out);
  nor nor_2 (nor_2_out, not_2_out, Y);
  nor nor_3 (nor_3_out, nor_1_out, nor_2_out);
  not not_3 (not_3_out, in_3);
  not not_4 (not_4_out, nor_1_out);
  not not_5 (not_5_out, nor_3_out);
  not not_6 (not_6_out, in_4);
  not not_7 (not_7_out, nor_2_out);
  not not_8 (not_8_out, in_5);
  nor nor_4 (x_y, not_3_out, not_4_out);
  nor nor_5 (x_y_2, not_5_out, not_6_out);
  nor nor_6 (x_y_3, not_7_out, not_8_out);
endmodule

module \Iterativna_šema  (
  input  [7:0] in_1,
  input  [7:0] in_2
);

  wire main_1_x_y_2, main_2_x_y_2, main_3_x_y_2, main_4_x_y_2, main_5_x_y_2, main_6_x_y_2;

  main main_1 (.Y(in_1[7]), .in_3(in_2[7]), .in_4(1'b1), .x_y_2(main_1_x_y_2));  // open: X, in_5, x_y, x_y_3
  main main_2 (.Y(in_1[6]), .in_3(in_2[6]), .in_4(main_1_x_y_2), .x_y_2(main_2_x_y_2));  // open: X, in_5, x_y, x_y_3
  main main_3 (.Y(in_1[5]), .in_3(in_2[5]), .in_4(main_2_x_y_2), .x_y_2(main_3_x_y_2));  // open: X, in_5, x_y, x_y_3
  main main_4 (.Y(in_2[4]), .in_3(in_1[4]), .in_4(main_3_x_y_2), .x_y_2(main_4_x_y_2));  // open: X, in_5, x_y, x_y_3
  main main_5 (.Y(in_1[3]), .in_3(in_2[3]), .in_4(main_4_x_y_2), .x_y_2(main_5_x_y_2));  // open: X, in_5, x_y, x_y_3
  main main_6 (.Y(in_1[2]), .in_3(in_2[2]), .in_4(main_5_x_y_2), .x_y_2(main_6_x_y_2));  // open: X, in_5, x_y, x_y_3
  main main_7 (.Y(in_2[1]), .in_3(in_1[1]), .in_4(main_6_x_y_2));  // open: X, in_5, x_y, x_y_2, x_y_3

  assign in_2[0] = in_1[0];
endmodule
