// Logisim project 4Zad.circ as structural Verilog: 1 circuit, main circuit 4.
module _4 (
  input  [3:0] Ulaz_4_bita,
  output [3:0] Izlaz
);

  wire decoder_1_out0, decoder_1_out1, decoder_1_out2, decoder_1_out3, decoder_1_out4, decoder_1_out5,
       decoder_1_out6, decoder_1_out7, decoder_1_out8, decoder_1_out9, decoder_1_out10, decoder_1_out11,
       decoder_1_out12, decoder_1_out13, decoder_1_out14, decoder_1_out15;

  Decoder #(.select(4), .enable("false")) decoder_1 (
    .out0(decoder_1_out0), .out1(decoder_1_out1), .out2(decoder_1_out2), .out3(decoder_1_out3),
    .out4(decoder_1_out4), .out5(decoder_1_out5), .out6(decoder_1_out6), .out7(decoder_1_out7),
    .out8(decoder_1_out8), .out9(decoder_1_out9), .out10(decoder_1_out10), .out11(decoder_1_out11),
    .out12(decoder_1_out12), .out13(decoder_1_out13), .out14(decoder_1_out14), .out15(decoder_1_out15),
    .sel(Ulaz_4_bita));
  or or_1 (Izlaz[3], decoder_1_out0, decoder_1_out1, decoder_1_out8, decoder_1_out9, decoder_1_out10);
  or or_2 (Izlaz[2], decoder_1_out1, decoder_1_out5, decoder_1_out6, decoder_1_out7, decoder_1_out8);
  or or_3 (Izlaz[1], decoder_1_out0, decoder_1_out3, decoder_1_out4, decoder_1_out7, decoder_1_out8, decoder_1_out11);
  or or_4 (Izlaz[0], decoder_1_out0, decoder_1_out2, decoder_1_out4, decoder_1_out6, decoder_1_out8, decoder_1_out10);

  // Notes on the sheet:
  //   ROM predstavlja dekoder sa I ili ILI kolima(U mom slucaju dekoder i 4 ili kola)
endmodule
