// Logisim project MO_Z3.circ as structural Verilog: 1 circuit, main circuit MO_Z2
module MO_Z2 (
);

  wire and_1_out, and_2_out, and_3_out, clock_1_out, Crveno_A, Crveno_P, d_ff_1_q, d_ff_2_q, d_ff_3_q,
       d_ff_4_q, d_ff_5_q, d_ff_6_q, d_ff_7_q, d_ff_8_q, d_ff_9_q, d_ff_10_q, d_ff_11_q, d_ff_12_q,
       d_ff_13_q, d_ff_14_q, d_ff_15_q, d_ff_16_q, d_ff_17_q, d_ff_18_q, d_ff_19_q, d_ff_20_q, d_ff_21_q,
       d_ff_22_q, d_ff_23_q, d_ff_24_q, Dugme_out, or_1_out, or_2_out, t_ff_1_q, t_ff_1_qn, t_ff_2_q,
       t_ff_2_qn, Zeleno_P;

  Button Dugme (.out(Dugme_out));
  Clock clock_1 (.out(clock_1_out));
  D_Flip_Flop d_ff_1 (.clk(clock_1_out), .D(Dugme_out), .Q(d_ff_1_q));  // open: Qn, preset, en, reset
  D_Flip_Flop d_ff_2 (.clk(clock_1_out), .D(d_ff_1_q), .Q(d_ff_2_q));  // open: Qn, preset, en, reset
  or or_1 (or_1_out, Dugme_out, d_ff_23_q, d_ff_19_q, d_ff_4_q);
  T_Flip_Flop t_ff_1 (.clk(or_1_out), .T(t_ff_2_q), .Q(t_ff_1_q), .Qn(t_ff_1_qn));  // open: preset, reset, en
  T_Flip_Flop t_ff_2 (.clk(or_1_out), .T(or_2_out), .Q(t_ff_2_q), .Qn(t_ff_2_qn));  // open: preset, reset, en
  or or_2 (or_2_out, t_ff_2_q, t_ff_1_q, Dugme_out);
  D_Flip_Flop d_ff_3 (.clk(clock_1_out), .D(d_ff_2_q), .Q(d_ff_3_q));  // open: Qn, preset, en, reset
  D_Flip_Flop d_ff_4 (.clk(clock_1_out), .D(d_ff_3_q), .Q(d_ff_4_q));  // open: Qn, preset, en, reset
  D_Flip_Flop d_ff_5 (.clk(clock_1_out), .D(d_ff_4_q), .Q(d_ff_5_q));  // open: Qn, preset, en, reset
  and and_1 (and_1_out, t_ff_1_qn, t_ff_2_q);
  and and_2 (and_2_out, t_ff_1_q, t_ff_2_qn);
  D_Flip_Flop d_ff_6 (.clk(clock_1_out), .D(d_ff_5_q), .Q(d_ff_6_q));  // open: Qn, preset, en, reset
  or or_3 (Crveno_A, and_1_out, and_2_out);
  LED led_1 (.in(Crveno_A));
  LED led_2 (.in(t_ff_2_q));
  and and_3 (and_3_out, t_ff_1_qn, t_ff_2_qn);
  LED led_3 (.in(and_3_out));
  and and_4 (Zeleno_P, t_ff_2_qn, t_ff_1_q);
  or or_4 (Crveno_P, t_ff_2_q, t_ff_1_qn);
  D_Flip_Flop d_ff_7 (.clk(clock_1_out), .D(d_ff_8_q), .Q(d_ff_7_q));  // open: Qn, preset, en, reset
  D_Flip_Flop d_ff_8 (.clk(clock_1_out), .D(d_ff_6_q), .Q(d_ff_8_q));  // open: Qn, preset, en, reset
  LED led_4 (.in(Crveno_P));
  LED led_5 (.in(Zeleno_P));
  D_Flip_Flop d_ff_9 (.clk(clock_1_out), .D(d_ff_7_q), .Q(d_ff_9_q));  // open: Qn, preset, en, reset
  D_Flip_Flop d_ff_10 (.clk(clock_1_out), .D(d_ff_9_q), .Q(d_ff_10_q));  // open: Qn, preset, en, reset
  D_Flip_Flop d_ff_11 (.clk(clock_1_out), .D(d_ff_12_q), .Q(d_ff_11_q));  // open: Qn, preset, en, reset
  D_Flip_Flop d_ff_12 (.clk(clock_1_out), .D(d_ff_10_q), .Q(d_ff_12_q));  // open: Qn, preset, en, reset
  D_Flip_Flop d_ff_13 (.clk(clock_1_out), .D(d_ff_11_q), .Q(d_ff_13_q));  // open: Qn, preset, en, reset
  D_Flip_Flop d_ff_14 (.clk(clock_1_out), .D(d_ff_13_q), .Q(d_ff_14_q));  // open: Qn, preset, en, reset
  D_Flip_Flop d_ff_15 (.clk(clock_1_out), .D(d_ff_14_q), .Q(d_ff_15_q));  // open: Qn, preset, en, reset
  D_Flip_Flop d_ff_16 (.clk(clock_1_out), .D(d_ff_15_q), .Q(d_ff_16_q));  // open: Qn, preset, en, reset
  D_Flip_Flop d_ff_17 (.clk(clock_1_out), .D(d_ff_16_q), .Q(d_ff_17_q));  // open: Qn, preset, en, reset
  D_Flip_Flop d_ff_18 (.clk(clock_1_out), .D(d_ff_17_q), .Q(d_ff_18_q));  // open: Qn, preset, en, reset
  D_Flip_Flop d_ff_19 (.clk(clock_1_out), .D(d_ff_20_q), .Q(d_ff_19_q));  // open: Qn, preset, en, reset
  D_Flip_Flop d_ff_20 (.clk(clock_1_out), .D(d_ff_18_q), .Q(d_ff_20_q));  // open: Qn, preset, en, reset
  D_Flip_Flop d_ff_21 (.clk(clock_1_out), .D(d_ff_19_q), .Q(d_ff_21_q));  // open: Qn, preset, en, reset
  D_Flip_Flop d_ff_22 (.clk(clock_1_out), .D(d_ff_21_q), .Q(d_ff_22_q));  // open: Qn, preset, en, reset
  D_Flip_Flop d_ff_23 (.clk(clock_1_out), .D(d_ff_24_q), .Q(d_ff_23_q));  // open: Qn, preset, en, reset
  D_Flip_Flop d_ff_24 (.clk(clock_1_out), .D(d_ff_22_q), .Q(d_ff_24_q));  // open: Qn, preset, en, reset
endmodule
