// Logisim project T9.circ as structural Verilog: 4 circuits, main circuit main
module main (
  input  [3:0] Adresa,
  input  [3:0] Adresa_2,
  input  Select,
  input  Select_2
);

  wire and_1_out, and_2_out, and_3_out, and_4_out, not_1_out, not_2_out, not_3_out, not_4_out;

  not not_1 (not_1_out, Select);
  not not_2 (not_2_out, Adresa[3]);
  and and_1 (and_1_out, not_2_out, not_1_out);
  and and_2 (and_2_out, Adresa[3], not_1_out);
  ROM #(.addrWidth(3), .dataWidth(2)) rom_1 (.addr(Adresa[2:0]), .sel(and_1_out));  // open: data
  ROM #(.addrWidth(3), .dataWidth(2)) rom_2 (.addr(Adresa[2:0]), .sel(and_2_out));  // open: data
  not not_3 (not_3_out, Select_2);
  not not_4 (not_4_out, Adresa_2[0]);
  and and_3 (and_3_out, not_4_out, not_3_out);
  and and_4 (and_4_out, Adresa_2[0], not_3_out);
  ROM #(.addrWidth(3), .dataWidth(2)) rom_3 (.addr(Adresa_2[3:1]), .sel(and_3_out));  // open: data
  ROM #(.addrWidth(3), .dataWidth(2)) rom_4 (.addr(Adresa_2[3:1]), .sel(and_4_out));  // open: data

  // Notes on the sheet:
  //   A2A1A0
  //   A3
  //   contents of rom_1 (hex, n*v repeats v):
  //   3 2 1 0 0 1 2 3
  //   contents of rom_2 (hex, n*v repeats v):
  //   3 2 1 0 0 1 2 3
  //   A0
  //   A3A2A1
  //   contents of rom_3 (hex, n*v repeats v):
  //   3 2 1
  //   contents of rom_4 (hex, n*v repeats v):
  //   3 2 1 0 0 1 2 3
endmodule

module Z1 (
  input  [3:0] Adresa,
  input  [3:0] Adresa_2,
  input  Select,
  input  Select_2,
  output [1:0] out_5,
  output [1:0] out_6
);

  wire and_1_out, and_2_out, and_3_out, and_4_out, not_1_out, not_2_out;

  not not_1 (not_1_out, Adresa[3]);
  and and_1 (and_1_out, not_1_out, Select);
  and and_2 (and_2_out, Adresa[3], Select);
  ROM #(.addrWidth(3), .dataWidth(2)) rom_1 (.addr(Adresa[2:0]), .data(out_5), .sel(and_1_out));
  ROM #(.addrWidth(3), .dataWidth(2)) rom_2 (.addr(Adresa[2:0]), .data(out_5), .sel(and_2_out));
  not not_2 (not_2_out, Adresa_2[0]);
  and and_3 (and_3_out, not_2_out, Select_2);
  and and_4 (and_4_out, Adresa_2[0], Select_2);
  ROM #(.addrWidth(3), .dataWidth(2)) rom_3 (.addr(Adresa_2[3:1]), .data(out_6), .sel(and_3_out));
  ROM #(.addrWidth(3), .dataWidth(2)) rom_4 (.addr(Adresa_2[3:1]), .data(out_6), .sel(and_4_out));

  // Notes on the sheet:
  //   A2A1A0
  //   A3
  //   contents of rom_1 (hex, n*v repeats v):
  //   3 2 1 0 0 1 2 3
  //   contents of rom_2 (hex, n*v repeats v):
  //   3 2 1 0 0 1 2 3
  //   A3A2A1
  //   A0
  //   contents of rom_3 (hex, n*v repeats v):
  //   3 2 1
  //   contents of rom_4 (hex, n*v repeats v):
  //   3 2 1 0 0 1 2 3
endmodule

module Z2 (
  input  [3:0] Adresa,
  input  Select,
  output [3:0] out_3
);

  wire decoder_1_out0, decoder_1_out1;

  Decoder decoder_1 (.out0(decoder_1_out0), .out1(decoder_1_out1), .sel(Adresa[3]), .en(Select));
  ROM #(.addrWidth(3), .dataWidth(2)) rom_1 (.addr(Adresa[2:0]), .data(out_3[1:0]), .sel(decoder_1_out0));
  ROM #(.addrWidth(3), .dataWidth(2)) rom_2 (.addr(Adresa[2:0]), .data(out_3[1:0]), .sel(decoder_1_out1));
  ROM #(.addrWidth(3), .dataWidth(2)) rom_3 (.addr(Adresa[2:0]), .data(out_3[3:2]), .sel(decoder_1_out0));
  ROM #(.addrWidth(3), .dataWidth(2)) rom_4 (.addr(Adresa[2:0]), .data(out_3[3:2]), .sel(decoder_1_out1));

  // Notes on the sheet:
  //   A3
  //   A2A1A0
  //   contents of rom_1 (hex, n*v repeats v):
  //   3 2 1 0 0 1 2 3
  //   contents of rom_2 (hex, n*v repeats v):
  //   3 1 4*2 1 3
  //   contents of rom_3 (hex, n*v repeats v):
  //   3 2 1 0 0 1 2 3
  //   contents of rom_4 (hex, n*v repeats v):
  //   3 2 1 0 0 1 2 3
endmodule

module brojac (
  output [3:0] out_1
);

  wire and_1_out, and_2_out, and_3_out, and_4_out, clock_1_out, n7_segment_display_driver_1_a_2,
       n7_segment_display_driver_1_b_2, n7_segment_display_driver_1_c_2, n7_segment_display_driver_1_d_2,
       n7_segment_display_driver_1_e, n7_segment_display_driver_1_f, n7_segment_display_driver_1_g, or_1_out,
       t_ff_1_q, t_ff_1_qn, t_ff_2_qn, t_ff_3_q, t_ff_3_qn;

  Clock clock_1 (.out(clock_1_out));
  and and_1 (and_1_out, out_1[1], t_ff_3_q);
  T_Flip_Flop t_ff_1 (.clk(clock_1_out), .T(or_1_out), .Q(t_ff_1_q), .Qn(t_ff_1_qn));  // open: preset, reset, en
  or or_1 (or_1_out, and_1_out, t_ff_1_q);
  T_Flip_Flop t_ff_2 (.clk(clock_1_out), .T(t_ff_3_q), .Q(out_1[1]), .Qn(t_ff_2_qn));  // open: preset, reset, en
  T_Flip_Flop t_ff_3 (.clk(clock_1_out), .T(t_ff_1_qn), .Q(t_ff_3_q), .Qn(t_ff_3_qn));  // open: preset, reset, en
  or or_2 (out_1[0], out_1[1], t_ff_3_qn);
  and and_2 (and_2_out, t_ff_3_q, out_1[1]);
  or or_3 (out_1[3], and_2_out, t_ff_1_q);
  and and_3 (and_3_out, out_1[1], t_ff_3_qn);
  or or_4 (out_1[2], and_3_out, t_ff_1_q, and_4_out);
  and and_4 (and_4_out, t_ff_2_qn, t_ff_3_q);
  _7_segment_display_driver u_7_segment_display_driver_1 (
    .D(out_1[3]), .C(out_1[2]), .B(out_1[1]), .A(out_1[0]), .a_2(n7_segment_display_driver_1_a_2),
    .b_2(n7_segment_display_driver_1_b_2), .c_2(n7_segment_display_driver_1_c_2),
    .d_2(n7_segment_display_driver_1_d_2), .e(n7_segment_display_driver_1_e),
    .f(n7_segment_display_driver_1_f), .g(n7_segment_display_driver_1_g));
  _7_Segment_Display u_7_segment_display_1 (
    .g(n7_segment_display_driver_1_g), .f(n7_segment_display_driver_1_f),
    .a(n7_segment_display_driver_1_a_2), .b(n7_segment_display_driver_1_b_2),
    .e(n7_segment_display_driver_1_e), .d(n7_segment_display_driver_1_d_2),
    .c(n7_segment_display_driver_1_c_2));  // open: dp
endmodule
