// Logisim project FullAdder.circ as structural Verilog: 5 circuits, main circuit main
module main (
  input  [7:0] in_1,
  input  [7:0] in_2,
  output [8:0] out_3
);

  wire fa_1bit_1_c_out, fa_1bit_2_c_out, fa_1bit_3_c_out, fa_1bit_4_c_out, fa_1bit_5_c_out, fa_1bit_6_c_out,
       fa_1bit_7_c_out;

  FA_1bit fa_1bit_1 (.A(in_1[0]), .B(in_2[0]), .C_in(1'b0), .C_out(fa_1bit_1_c_out), .S(out_3[0]));
  FA_1bit fa_1bit_2 (.A(in_1[1]), .B(in_2[1]), .C_in(fa_1bit_1_c_out), .C_out(fa_1bit_2_c_out), .S(out_3[1]));
  FA_1bit fa_1bit_3 (.A(in_1[2]), .B(in_2[2]), .C_in(fa_1bit_2_c_out), .C_out(fa_1bit_3_c_out), .S(out_3[2]));
  FA_1bit fa_1bit_4 (.A(in_1[3]), .B(in_2[3]), .C_in(fa_1bit_3_c_out), .C_out(fa_1bit_4_c_out), .S(out_3[3]));
  FA_1bit fa_1bit_5 (.A(in_1[4]), .B(in_2[4]), .C_in(fa_1bit_4_c_out), .C_out(fa_1bit_5_c_out), .S(out_3[4]));
  FA_1bit fa_1bit_6 (.A(in_1[5]), .B(in_2[5]), .C_in(fa_1bit_5_c_out), .C_out(fa_1bit_6_c_out), .S(out_3[5]));
  FA_1bit fa_1bit_7 (.A(in_1[6]), .B(in_2[6]), .C_in(fa_1bit_6_c_out), .C_out(fa_1bit_7_c_out), .S(out_3[6]));
  FA_1bit fa_1bit_8 (.A(in_1[7]), .B(in_2[7]), .C_in(fa_1bit_7_c_out), .C_out(out_3[8]), .S(out_3[7]));
endmodule

// 1bit sabirac
module FA_1bit (
  input  A,
  input  B,
  input  C_in,
  output S,
  output C_out
);

  wire and_1_out, not_1_out, or_1_out, xor_1_out;

  xor xor_1 (xor_1_out, A, B);
  and and_1 (and_1_out, A, B);
  or or_1 (or_1_out, A, B);
  Multiplexer #(.enable("false")) multiplexer_1 (.in0(xor_1_out), .in1(not_1_out), .out(S), .sel(C_in));
  not not_1 (not_1_out, xor_1_out);
  Multiplexer #(.enable("false")) multiplexer_2 (.in0(and_1_out), .in1(or_1_out), .out(C_out), .sel(C_in));
endmodule

module FA_1bit_4x1Mux (
  input  C_in,
  input  A,
  input  B,
  output S,
  output C_out
);

  wire not_1_out;

  not not_1 (not_1_out, C_in);
  Multiplexer #(.select(2), .enable("false")) multiplexer_1 (
    .in0(C_in), .in1(not_1_out), .in2(not_1_out), .in3(C_in), .out(S), .sel({B, A}));
  Multiplexer #(.select(2), .enable("false")) multiplexer_2 (
    .in0(1'b0), .in1(C_in), .in2(C_in), .in3(1'b1), .out(C_out), .sel({B, A}));
  FA_1bit fa_1bit_1 ();  // open: A, B, C_in, C_out, S
endmodule

module FA_1bit_elemComp (
  input  A,
  input  B,
  input  C_in,
  output S,
  output C_out
);

  wire and_1_out, and_2_out, and_3_out, xor_1_out;

  xor xor_1 (xor_1_out, A, B);
  and and_1 (and_1_out, A, B);
  and and_2 (and_2_out, A, C_in);
  and and_3 (and_3_out, B, C_in);
  xor xor_2 (S, xor_1_out, C_in);
  or or_1 (C_out, and_1_out, and_2_out, and_3_out);
endmodule

module FA_1bit_8x1Mux (
  input  A,
  input  B,
  input  C_in,
  output S,
  output C_out
);

  Multiplexer #(.select(3), .enable("false")) multiplexer_1 (
    .in0(1'b0), .in1(1'b1), .in2(1'b1), .in3(1'b0), .in4(1'b1), .in5(1'b0), .in6(1'b0), .in7(1'b1), .out(S),
    .sel({A, B, C_in}));
  Multiplexer #(.select(3), .enable("false")) multiplexer_2 (
    .in0(1'b0), .in1(1'b0), .in2(1'b0), .in3(1'b1), .in4(1'b0), .in5(1'b1), .in6(1'b1), .in7(1'b1),
    .out(C_out), .sel({A, B, C_in}));
endmodule
