// Logisim project GrayToBinary.circ as structural Verilog: 2 circuits, main circuit 4bit GrayToBinary
// 4bitGrtoBi
module _4bit_GrayToBinary (
  input  g0,
  input  g1,
  input  g2,
  input  g3,
  input  b4,
  output b0,
  output b1,
  output b3,
  output b4_2
);

  wire not_1_out, not_2_out, not_3_out, not_4_out;

  not not_1 (not_1_out, g0);
  not not_2 (not_2_out, g1);
  not not_3 (not_3_out, g2);
  not not_4 (not_4_out, g3);
  Multiplexer #(.enable("false")) multiplexer_1 (.in0(g0), .in1(not_1_out), .out(b0), .sel(b1));
  Multiplexer #(.enable("false")) multiplexer_2 (.in0(g1), .in1(not_2_out), .out(b1), .sel(b3));
  Multiplexer #(.enable("false")) multiplexer_3 (.in0(g2), .in1(not_3_out), .out(b3), .sel(b4_2));
  Multiplexer #(.enable("false")) multiplexer_4 (.in0(g3), .in1(not_4_out), .out(b4_2), .sel(b4));
endmodule

module _8bit_GrayToBinary (
  input  g0,
  input  g1,
  input  g2,
  input  g3,
  input  g4,
  input  g5,
  input  g6,
  input  g7,
  input  b8,
  output b0,
  output b1,
  output b2,
  output b3,
  output b4,
  output b5,
  output b6,
  output b7
);

  _4bit_GrayToBinary u_4bit_graytobinary_1 (
    .g0(g0), .g1(g1), .g2(g2), .g3(g3), .b4(b4), .b0(b0), .b1(b1), .b3(b2), .b4_2(b3));
  _4bit_GrayToBinary u_4bit_graytobinary_2 (
    .g0(g4), .g1(g4), .g2(g6), .g3(g7), .b4(b8), .b0(b4), .b1(b5), .b3(b6), .b4_2(b7));

  assign g5 = g4;
endmodule
