// Logisim project Zadatak2_svi.circ as structural Verilog: 4 circuits, main circuit a
module a (
  output [3:0] Izlaz
);

  wire and_1_out, and_2_out, and_4_out, and_5_out, and_6_out, and_7_out, D0_q, D0_qn, D1_q, D2_q, D2_qn,
       or_1_out, or_2_out, Sat_out;

  Clock Sat (.out(Sat_out));
  and and_1 (and_1_out, D0_q, D2_qn);
  or or_1 (or_1_out, and_1_out, and_2_out, Izlaz[2]);
  and and_2 (and_2_out, D0_qn, D2_q);
  and and_3 (Izlaz[3], D2_q, D1_q);
  D_Flip_Flop D2 (.clk(Sat_out), .D(or_1_out), .Q(D2_q), .Qn(D2_qn));  // open: preset, en, reset
  D_Flip_Flop D1 (.clk(Sat_out), .D(or_2_out), .Q(D1_q), .Qn(Izlaz[2]));  // open: preset, en, reset
  or or_2 (or_2_out, and_5_out, and_4_out);
  and and_4 (and_4_out, D0_qn, D1_q);
  and and_5 (and_5_out, D2_q, D0_q);
  D_Flip_Flop D0 (.clk(Sat_out), .D(D0_qn), .Q(D0_q), .Qn(D0_qn));  // open: preset, en, reset
  and and_6 (and_6_out, D2_q, D1_q);
  or or_3 (Izlaz[1], and_6_out, D0_q);
  and and_7 (and_7_out, D0_q, D1_q);
  or or_4 (Izlaz[0], and_7_out, D2_qn);
endmodule

module b (
  output [3:0] Izlaz
);

  wire and_1_out, and_3_out, and_4_out, and_5_out, and_6_out, clock_1_out, or_1_out, Q0_q, Q1_q, Q2_q, Q2_qn;

  Clock clock_1 (.out(clock_1_out));
  and and_1 (and_1_out, Q0_q, Q1_q);
  and and_2 (Izlaz[3], Q2_q, Q1_q);
  T_Flip_Flop Q2 (.clk(clock_1_out), .T(and_1_out), .Q(Q2_q), .Qn(Q2_qn));  // open: preset, reset, en
  or or_1 (or_1_out, and_3_out, and_4_out);
  and and_3 (and_3_out, Q2_qn, Q0_q);
  and and_4 (and_4_out, Izlaz[2], Q0_q);
  T_Flip_Flop Q1 (.clk(clock_1_out), .T(or_1_out), .Q(Q1_q), .Qn(Izlaz[2]));  // open: preset, reset, en
  and and_5 (and_5_out, Q2_q, Q1_q);
  or or_2 (Izlaz[1], and_5_out, Q0_q);
  T_Flip_Flop Q0 (.clk(clock_1_out), .T(1'b1), .Q(Q0_q));  // open: Qn, preset, reset, en
  and and_6 (and_6_out, Q1_q, Q0_q);
  or or_3 (Izlaz[0], and_6_out, Q2_qn);
endmodule

module c (
  output [3:0] Izlaz
);

  wire and_1_out, and_2_out, and_4_out, and_5_out, and_6_out, and_7_out, clock_1_out, RS0_q, RS0_qn, RS1_q,
       RS2_q, RS2_qn;

  Clock clock_1 (.out(clock_1_out));
  and and_1 (and_1_out, RS0_q, RS2_qn);
  and and_2 (and_2_out, RS0_q, RS1_q, RS2_q);
  S_R_Flip_Flop RS2 (
    .S(and_1_out), .clk(clock_1_out), .R(and_2_out), .Q(RS2_q), .Qn(RS2_qn));  // open: preset, reset, en
  and and_3 (Izlaz[3], RS1_q, RS2_q);
  and and_4 (and_4_out, RS0_q, Izlaz[2]);
  and and_5 (and_5_out, RS2_qn, RS0_q);
  S_R_Flip_Flop RS1 (
    .S(and_4_out), .clk(clock_1_out), .R(and_5_out), .Q(RS1_q), .Qn(Izlaz[2]));  // open: preset, reset, en
  and and_6 (and_6_out, RS1_q, RS2_q);
  or or_1 (Izlaz[1], and_6_out, RS0_q);
  S_R_Flip_Flop RS0 (.S(RS0_qn), .clk(clock_1_out), .R(RS0_q), .Q(RS0_q), .Qn(RS0_qn));  // open: preset, reset, en
  and and_7 (and_7_out, RS1_q, RS0_q);
  or or_2 (Izlaz[0], and_7_out, RS2_qn);
endmodule

module d (
  output [3:0] Izlaz
);

  wire and_1_out, and_3_out, and_4_out, and_5_out, clock_1_out, j_k_ff_1_q, j_k_ff_1_qn, j_k_ff_2_q,
       j_k_ff_3_q;

  Clock clock_1 (.out(clock_1_out));
  and and_1 (and_1_out, j_k_ff_3_q, j_k_ff_2_q);
  J_K_Flip_Flop j_k_ff_1 (
    .J(j_k_ff_3_q), .clk(clock_1_out), .K(and_1_out), .Q(j_k_ff_1_q), .Qn(j_k_ff_1_qn));  // open: preset, en, reset
  and and_2 (Izlaz[3], j_k_ff_2_q, j_k_ff_1_q);
  and and_3 (and_3_out, j_k_ff_1_qn, j_k_ff_3_q);
  J_K_Flip_Flop j_k_ff_2 (
    .J(j_k_ff_3_q), .clk(clock_1_out), .K(and_3_out), .Q(j_k_ff_2_q), .Qn(Izlaz[2]));  // open: preset, en, reset
  and and_4 (and_4_out, j_k_ff_2_q, j_k_ff_1_q);
  or or_1 (Izlaz[1], and_4_out, j_k_ff_3_q);
  J_K_Flip_Flop j_k_ff_3 (.J(1'b1), .clk(clock_1_out), .K(1'b1), .Q(j_k_ff_3_q));  // open: Qn, preset, en, reset
  and and_5 (and_5_out, j_k_ff_2_q, j_k_ff_3_q);
  or or_2 (Izlaz[0], and_5_out, j_k_ff_1_qn);
endmodule
