// Logisim project Zadatak3.circ as structural Verilog: 2 circuits, main circuit a
module a (
  input  X,
  output Y
);

  wire and_1_out, and_2_out, or_1_out, or_2_out, Sat_out, T0_q, T1_q, T1_qn;

  Clock Sat (.out(Sat_out));
  or or_1 (or_1_out, and_1_out, T1_q);
  and and_1 (and_1_out, X, T0_q);
  T_Flip_Flop T1 (.clk(Sat_out), .T(or_1_out), .Q(T1_q), .Qn(T1_qn));  // open: preset, reset, en
  or or_2 (or_2_out, and_2_out, T0_q);
  and and_2 (and_2_out, T1_qn, X);
  T_Flip_Flop T0 (.clk(Sat_out), .T(or_2_out), .Q(T0_q));  // open: Qn, preset, reset, en
  and and_3 (Y, T1_q, X);
endmodule

module b (
  input  X,
  output Y
);

  wire and_1_out, and_2_out, not_1_out, or_1_out, or_2_out, Sat_out, T0_q, T1_q, T1_qn;

  Clock Sat (.out(Sat_out));
  T_Flip_Flop T1 (.clk(Sat_out), .T(or_1_out), .Q(T1_q), .Qn(T1_qn));  // open: preset, reset, en
  or or_1 (or_1_out, and_1_out, and_2_out);
  and and_1 (and_1_out, T1_q, not_1_out);
  and and_2 (and_2_out, X, T1_qn, T0_q);
  not not_1 (not_1_out, X);
  or or_2 (or_2_out, T0_q, X);
  T_Flip_Flop T0 (.clk(Sat_out), .T(or_2_out), .Q(T0_q));  // open: Qn, preset, reset, en
  and and_3 (Y, T0_q, T1_q);
endmodule
