// Logisim project Zadatak_1.circ as structural Verilog: 3 circuits, main circuit a
module a (
  input  D,
  output Q,
  output Q_prime
);

  wire not_1_out, Signal_Sata_out;

  Clock Signal_Sata (.out(Signal_Sata_out));
  not not_1 (not_1_out, D);
  S_R_Flip_Flop s_r_ff_1 (.S(D), .clk(Signal_Sata_out), .R(not_1_out), .Q(Q), .Qn(Q_prime));  // open: preset, reset, en
endmodule

module b (
  input  T,
  output Q,
  output Q_prime
);

  wire and_1_out, and_2_out, not_1_out, not_2_out, or_1_out, Signal_Sata_out;

  Clock Signal_Sata (.out(Signal_Sata_out));
  not not_1 (not_1_out, T);
  and and_1 (and_1_out, Q, not_1_out);
  and and_2 (and_2_out, T, not_2_out);
  or or_1 (or_1_out, and_1_out, and_2_out);
  not not_2 (not_2_out, Q);
  D_Flip_Flop d_ff_1 (.clk(Signal_Sata_out), .D(or_1_out), .Q(Q), .Qn(Q_prime));  // open: preset, en, reset
endmodule

module c (
  input  J,
  input  K,
  output Q,
  output Q_prime
);

  wire and_1_out, and_2_out, or_1_out, Signal_Sata_out;

  Clock Signal_Sata (.out(Signal_Sata_out));
  and and_1 (and_1_out, Q_prime, J);
  and and_2 (and_2_out, K, Q);
  T_Flip_Flop t_ff_1 (.clk(Signal_Sata_out), .T(or_1_out), .Q(Q), .Qn(Q_prime));  // open: preset, reset, en
  or or_1 (or_1_out, and_1_out, and_2_out);
endmodule
