// Logisim project Z2.circ as structural Verilog: 1 circuit, main circuit main
module main (
  input  A,
  input  B,
  input  C,
  input  D,
  output Y1,
  output Y2
);

  wire and_1_out, and_2_out, and_3_out, and_4_out, and_5_out, and_6_out, and_7_out, and_8_out, and_9_out,
       and_10_out, and_11_out, and_12_out, and_13_out, and_14_out, not_1_out, not_2_out, not_3_out, not_4_out;

  not not_1 (not_1_out, A);
  not not_2 (not_2_out, B);
  not not_3 (not_3_out, C);
  not not_4 (not_4_out, D);
  and and_1 (and_1_out, not_1_out, not_2_out, not_3_out, not_4_out);
  and and_2 (and_2_out, not_1_out, not_2_out, C, not_4_out);
  and and_3 (and_3_out, not_1_out, B, not_3_out, not_4_out);
  and and_4 (and_4_out, not_1_out, not_2_out, not_3_out, not_4_out);
  and and_5 (and_5_out, not_1_out, B, C, not_4_out);
  and and_6 (and_6_out, not_1_out, not_2_out, C, D);
  and and_7 (and_7_out, A, not_2_out, not_3_out, not_4_out);
  and and_8 (and_8_out, not_1_out, B, C, not_4_out);
  and and_9 (and_9_out, A, B, not_3_out, not_4_out);
  and and_10 (and_10_out, A, not_2_out, C, not_4_out);
  and and_11 (and_11_out, A, B, not_3_out, not_4_out);
  and and_12 (and_12_out, A, not_2_out, not_3_out, D);
  and and_13 (and_13_out, A, B, C, not_4_out);
  and and_14 (and_14_out, A, B, C, D);
  or or_1 (Y1, and_1_out, and_2_out, and_3_out, and_5_out, and_7_out, and_10_out, and_9_out, and_13_out);
  or or_2 (Y2, and_14_out, and_11_out, and_12_out, and_8_out, and_6_out, and_4_out);

  // Notes on the sheet:
  //   4 bitni ulaz: 
  //   A'B'C'D'
  //   A'BC'D'
  //   A'B'CD
  //   A'B'C'D'
  //   A'BCD'
  //   A'B'CD
  //   a)Funkcija Y1: Izlaz je tacan samo ako je ulaz djeljiv sa 2
  //   AB'CD'
  //   AB'C'D'
  //   AB'C'D
  //   A'BCD'
  //   b)Funkcija Y2: Izlaz je tacan samo ako je ulaz djeljiv sa 3
  //   ABC'D'
  //   ABC'D'
  //   ABCD'
  //   ABCD
endmodule
