// Logisim project Z3.circ as structural Verilog: 1 circuit, main circuit main
module main (
  input  A,
  input  B,
  input  C,
  output Y
);

  wire and_1_out, not_1_out, not_2_out, not_3_out;

  not not_1 (not_1_out, A);
  not not_2 (not_2_out, B);
  not not_3 (not_3_out, C);
  and and_1 (and_1_out, not_2_out, not_3_out);
  or or_1 (Y, not_1_out, and_1_out);

  // Notes on the sheet:
  //   B'C'
  //   Funkcija koja je tacna samo ako je ulaz manji od 5
  //   A' V B'C'
endmodule
