// Logisim project Z4.circ as structural Verilog: 1 circuit, main circuit main
module main (
  input  S0,
  input  S1,
  input  S2,
  input  D0,
  input  D1,
  input  D2,
  input  D3,
  input  D4,
  input  D5,
  input  D6,
  input  D7,
  input  Ulaz1,
  input  Upravljacki_Signal,
  input  Ulaz2,
  output Q0,
  output Q1,
  output Q2,
  output Q3,
  output Q4,
  output Q5,
  output Q6,
  output Q7,
  output Izlaz
);

  wire multiplexer_1_out, multiplexer_2_out, multiplexer_3_out, multiplexer_4_out, multiplexer_5_out,
       multiplexer_6_out, multiplexer_7_out, multiplexer_8_out, multiplexer_9_out, multiplexer_10_out,
       multiplexer_11_out, multiplexer_12_out, multiplexer_13_out, multiplexer_14_out, multiplexer_15_out,
       multiplexer_16_out, nand_1_out, nand_2_out, nand_3_out;

  Multiplexer #(.disabled(0), .enable("false")) multiplexer_1 (.in0(D0), .in1(D7), .out(multiplexer_1_out), .sel(S0));
  Multiplexer #(.disabled(0), .enable("false")) multiplexer_2 (.in0(D1), .in1(D0), .out(multiplexer_2_out), .sel(S0));
  Multiplexer #(.disabled(0), .enable("false")) multiplexer_3 (.in0(D2), .in1(D1), .out(multiplexer_3_out), .sel(S0));
  Multiplexer #(.disabled(0), .enable("false")) multiplexer_4 (.in0(D3), .in1(D2), .out(multiplexer_4_out), .sel(S0));
  Multiplexer #(.disabled(0), .enable("false")) multiplexer_5 (.in0(D4), .in1(D3), .out(multiplexer_5_out), .sel(S0));
  Multiplexer #(.disabled(0), .enable("false")) multiplexer_6 (.in0(D5), .in1(D4), .out(multiplexer_6_out), .sel(S0));
  Multiplexer #(.disabled(0), .enable("false")) multiplexer_7 (.in0(D6), .in1(D5), .out(multiplexer_7_out), .sel(S0));
  Multiplexer #(.disabled(0), .enable("false")) multiplexer_8 (.in0(D7), .in1(D6), .out(multiplexer_8_out), .sel(S0));
  nand nand_1 (nand_1_out, Upravljacki_Signal, Upravljacki_Signal);
  Multiplexer #(.disabled(0), .enable("false")) multiplexer_9 (
    .in0(multiplexer_1_out), .in1(multiplexer_7_out), .out(multiplexer_9_out), .sel(S1));
  Multiplexer #(.disabled(0), .enable("false")) multiplexer_10 (
    .in0(multiplexer_2_out), .in1(multiplexer_8_out), .out(multiplexer_10_out), .sel(S1));
  Multiplexer #(.disabled(0), .enable("false")) multiplexer_11 (
    .in0(multiplexer_3_out), .in1(multiplexer_1_out), .out(multiplexer_11_out), .sel(S1));
  Multiplexer #(.disabled(0), .enable("false")) multiplexer_12 (
    .in0(multiplexer_4_out), .in1(multiplexer_2_out), .out(multiplexer_12_out), .sel(S1));
  Multiplexer #(.disabled(0), .enable("false")) multiplexer_13 (
    .in0(multiplexer_5_out), .in1(multiplexer_3_out), .out(multiplexer_13_out), .sel(S1));
  Multiplexer #(.disabled(0), .enable("false")) multiplexer_14 (
    .in0(multiplexer_6_out), .in1(multiplexer_4_out), .out(multiplexer_14_out), .sel(S1));
  Multiplexer #(.disabled(0), .enable("false")) multiplexer_15 (
    .in0(multiplexer_7_out), .in1(multiplexer_5_out), .out(multiplexer_15_out), .sel(S1));
  Multiplexer #(.disabled(0), .enable("false")) multiplexer_16 (
    .in0(multiplexer_8_out), .in1(multiplexer_6_out), .out(multiplexer_16_out), .sel(S1));
  nand nand_2 (nand_2_out, Ulaz1, Upravljacki_Signal);
  nand nand_3 (nand_3_out, nand_1_out, Ulaz2);
  Multiplexer #(.disabled(0), .enable("false")) multiplexer_17 (
    .in0(multiplexer_9_out), .in1(multiplexer_13_out), .out(Q0), .sel(S2));
  Multiplexer #(.disabled(0), .enable("false")) multiplexer_18 (
    .in0(multiplexer_10_out), .in1(multiplexer_14_out), .out(Q1), .sel(S2));
  Multiplexer #(.disabled(0), .enable("false")) multiplexer_19 (
    .in0(multiplexer_11_out), .in1(multiplexer_15_out), .out(Q2), .sel(S2));
  Multiplexer #(.disabled(0), .enable("false")) multiplexer_20 (
    .in0(multiplexer_12_out), .in1(multiplexer_16_out), .out(Q3), .sel(S2));
  Multiplexer #(.disabled(0), .enable("false")) multiplexer_21 (
    .in0(multiplexer_13_out), .in1(multiplexer_9_out), .out(Q4), .sel(S2));
  Multiplexer #(.disabled(0), .enable("false")) multiplexer_22 (
    .in0(multiplexer_14_out), .in1(multiplexer_10_out), .out(Q5), .sel(S2));
  Multiplexer #(.disabled(0), .enable("false")) multiplexer_23 (
    .in0(multiplexer_15_out), .in1(multiplexer_11_out), .out(Q6), .sel(S2));
  Multiplexer #(.disabled(0), .enable("false")) multiplexer_24 (
    .in0(multiplexer_16_out), .in1(multiplexer_12_out), .out(Q7), .sel(S2));
  nand nand_4 (Izlaz, nand_2_out, nand_3_out);

  // Notes on the sheet:
  //   Ulazi
  //   Unutrasnji izgled Multipleksera
  //   Koristit cemo gotov multiplexer (MUX) radi jednostavnosti
  //   Upravljacki Signali
  //   Izlazi
endmodule
