// Logisim project Z5.circ as structural Verilog: 1 circuit, main circuit 4 bitni poptupni sabirac (MUX 2to1)
// 4bit sabirac
module _4_bitni_poptupni_sabirac__MUX_2to1 (
  input  B3,
  input  B2,
  input  B1,
  input  B0,
  input  A3,
  input  A2,
  input  A1,
  input  A0,
  input  C_in,
  output S0,
  output S1,
  output S2,
  output S3,
  output C_out
);

  wire and_1_out, and_2_out, and_3_out, and_4_out, multiplexer_2_out, multiplexer_4_out, multiplexer_6_out,
       not_1_out, not_2_out, not_3_out, not_4_out, or_1_out, or_2_out, or_3_out, or_4_out, xor_1_out,
       xor_2_out, xor_3_out, xor_4_out;

  xor xor_1 (xor_1_out, A0, B0);
  and and_1 (and_1_out, A0, B0);
  or or_1 (or_1_out, A0, B0);
  xor xor_2 (xor_2_out, A1, B1);
  and and_2 (and_2_out, A1, B1);
  or or_2 (or_2_out, A1, B1);
  xor xor_3 (xor_3_out, A2, B2);
  and and_3 (and_3_out, A2, B2);
  or or_3 (or_3_out, A2, B2);
  xor xor_4 (xor_4_out, A3, B3);
  and and_4 (and_4_out, A3, B3);
  or or_4 (or_4_out, A3, B3);
  Multiplexer #(.enable("false")) multiplexer_1 (.in0(xor_1_out), .in1(not_1_out), .out(S0), .sel(C_in));
  not not_1 (not_1_out, xor_1_out);
  Multiplexer #(.enable("false")) multiplexer_2 (.in0(and_1_out), .in1(or_1_out), .out(multiplexer_2_out), .sel(C_in));
  Multiplexer #(.enable("false")) multiplexer_3 (.in0(xor_2_out), .in1(not_2_out), .out(S1), .sel(multiplexer_2_out));
  not not_2 (not_2_out, xor_2_out);
  Multiplexer #(.enable("false")) multiplexer_4 (
    .in0(and_2_out), .in1(or_2_out), .out(multiplexer_4_out), .sel(multiplexer_2_out));
  Multiplexer #(.enable("false")) multiplexer_5 (.in0(xor_3_out), .in1(not_3_out), .out(S2), .sel(multiplexer_4_out));
  not not_3 (not_3_out, xor_3_out);
  Multiplexer #(.enable("false")) multiplexer_6 (
    .in0(and_3_out), .in1(or_3_out), .out(multiplexer_6_out), .sel(multiplexer_4_out));
  Multiplexer #(.enable("false")) multiplexer_7 (.in0(xor_4_out), .in1(not_4_out), .out(S3), .sel(multiplexer_6_out));
  not not_4 (not_4_out, xor_4_out);
  Multiplexer #(.enable("false")) multiplexer_8 (.in0(and_4_out), .in1(or_4_out), .out(C_out), .sel(multiplexer_6_out));

  // Notes on the sheet:
  //   Ulaz1
  //   Ulaz2
  //   Ulaz1
  //   Ulaz2
  //   Ulaz1
  //   Ulaz2
  //   Ulaz1
  //   Ulaz2
  //   4 bitni potpuni sabirac
  //   Jednobitni sabirac pomocu mux-a
  //   Izlaz
  //   Izlaz
  //   Izlaz
  //   Izlaz
  //   Prenos
  //   Za realizaciju 4bitnog potpunog sabiraca
  //   Koristit cemo 4 jednobitna potpuna sabiraca
endmodule
