// Logisim project Z1.circ as structural Verilog: 5 circuits, main circuit a)8x32
// 8x32
module a_8x32 (
  input  [2:0] Input,
  input  Select,
  input  Write,
  output [31:0] Output
);

  RAM #(.addrWidth(3)) ram_1 (.addr(Input), .data(Output[7:0]), .sel(Select), .ld(Write));  // open: clk, clr
  RAM #(.addrWidth(3)) ram_2 (.addr(Input), .data(Output[15:8]), .sel(Select), .ld(Write));  // open: clk, clr
  RAM #(.addrWidth(3)) ram_3 (.addr(Input), .data(Output[23:16]), .sel(Select), .ld(Write));  // open: clk, clr
  RAM #(.addrWidth(3)) ram_4 (.addr(Input), .data(Output[31:24]), .sel(Select), .ld(Write));  // open: clk, clr
endmodule

module a_64x32 (
  input  [5:0] Input,
  input  Enable,
  output [31:0] Output
);

  wire decoder_1_out0, decoder_1_out1, decoder_1_out2, decoder_1_out3, decoder_1_out4, decoder_1_out5,
       decoder_1_out6, decoder_1_out7;

  Decoder #(.select(3), .enable("false")) decoder_1 (
    .out0(decoder_1_out0), .out1(decoder_1_out1), .out2(decoder_1_out2), .out3(decoder_1_out3),
    .out4(decoder_1_out4), .out5(decoder_1_out5), .out6(decoder_1_out6), .out7(decoder_1_out7),
    .sel(Input[5:3]));
  a_8x32 a_8x32_1 (.Input(Input[2:0]), .Select(decoder_1_out0), .Write(Enable), .Output(Output));
  a_8x32 a_8x32_2 (.Input(Input[2:0]), .Select(decoder_1_out1), .Write(Enable), .Output(Output));
  a_8x32 a_8x32_3 (.Input(Input[2:0]), .Select(decoder_1_out2), .Write(Enable), .Output(Output));
  a_8x32 a_8x32_4 (.Input(Input[2:0]), .Select(decoder_1_out3), .Write(Enable), .Output(Output));
  a_8x32 a_8x32_5 (.Input(Input[2:0]), .Select(decoder_1_out4), .Write(Enable), .Output(Output));
  a_8x32 a_8x32_6 (.Input(Input[2:0]), .Select(decoder_1_out5), .Write(Enable), .Output(Output));
  a_8x32 a_8x32_7 (.Input(Input[2:0]), .Select(decoder_1_out6), .Write(Enable), .Output(Output));
  a_8x32 a_8x32_8 (.Input(Input[2:0]), .Select(decoder_1_out7), .Write(Enable), .Output(Output));
endmodule

// 32x64
module b_32Mx64 (
  input  [4:0] Input,
  input  Select,
  input  Load,
  output [31:0] Output_first_32,
  output [31:0] Output_last_32
);

  RAM #(.addrWidth(5), .dataWidth(32)) ram_1 (
    .addr(Input), .data(Output_first_32), .sel(Select), .ld(Load));  // open: clk, clr
  RAM #(.addrWidth(5), .dataWidth(32)) ram_2 (
    .addr(Input), .data(Output_last_32), .sel(Select), .ld(Load));  // open: clk, clr
endmodule

// 1Gx64
module b_1Gx64 (
  input  [9:0] Input,
  input  Load,
  input  Select,
  output [31:0] output_last_32,
  output [31:0] Output_first_32
);

  wire _1, _2, _3, _4, _5, _6, _7, _8, _9, _10, _11, _12, _13, _14, _15, _16, _17, _18, _19, _20, _21, _22,
       _23, _24, _25, _26, _27, _28, _29, _30, _31, _32;

  Decoder #(.select(5)) decoder_1 (
    .out0(_1), .out1(_2), .out2(_3), .out3(_4), .out4(_5), .out5(_6), .out6(_7), .out7(_8), .out8(_9),
    .out9(_10), .out10(_11), .out11(_12), .out12(_13), .out13(_14), .out14(_15), .out15(_16), .out16(_17),
    .out17(_18), .out18(_19), .out19(_20), .out20(_21), .out21(_22), .out22(_23), .out23(_24), .out24(_25),
    .out25(_26), .out26(_27), .out27(_28), .out28(_29), .out29(_30), .out30(_31), .out31(_32),
    .sel(Input[9:5]), .en(Select));
  b_32Mx64 b_32mx64_1 (
    .Input(Input[4:0]), .Select(_1), .Load(Load), .Output_first_32(Output_first_32),
    .Output_last_32(output_last_32));
  b_32Mx64 b_32mx64_2 (
    .Input(Input[4:0]), .Select(_2), .Load(Load), .Output_first_32(Output_first_32),
    .Output_last_32(output_last_32));
  b_32Mx64 b_32mx64_3 (
    .Input(Input[4:0]), .Select(_3), .Load(Load), .Output_first_32(Output_first_32),
    .Output_last_32(output_last_32));
  b_32Mx64 b_32mx64_4 (
    .Input(Input[4:0]), .Select(_4), .Load(Load), .Output_first_32(Output_first_32),
    .Output_last_32(output_last_32));
  b_32Mx64 b_32mx64_5 (
    .Input(Input[4:0]), .Select(_5), .Load(Load), .Output_first_32(Output_first_32),
    .Output_last_32(output_last_32));
  b_32Mx64 b_32mx64_6 (
    .Input(Input[4:0]), .Select(_6), .Load(Load), .Output_first_32(Output_first_32),
    .Output_last_32(output_last_32));
  b_32Mx64 b_32mx64_7 (
    .Input(Input[4:0]), .Select(_7), .Load(Load), .Output_first_32(Output_first_32),
    .Output_last_32(output_last_32));
  b_32Mx64 b_32mx64_8 (
    .Input(Input[4:0]), .Select(_8), .Load(Load), .Output_first_32(Output_first_32),
    .Output_last_32(output_last_32));
  b_32Mx64 b_32mx64_9 (
    .Input(Input[4:0]), .Select(_9), .Load(Load), .Output_first_32(Output_first_32),
    .Output_last_32(output_last_32));
  b_32Mx64 b_32mx64_10 (
    .Input(Input[4:0]), .Select(_10), .Load(Load), .Output_first_32(Output_first_32),
    .Output_last_32(output_last_32));
  b_32Mx64 b_32mx64_11 (
    .Input(Input[4:0]), .Select(_11), .Load(Load), .Output_first_32(Output_first_32),
    .Output_last_32(output_last_32));
  b_32Mx64 b_32mx64_12 (
    .Input(Input[4:0]), .Select(_12), .Load(Load), .Output_first_32(Output_first_32),
    .Output_last_32(output_last_32));
  b_32Mx64 b_32mx64_13 (
    .Input(Input[4:0]), .Select(_13), .Load(Load), .Output_first_32(Output_first_32),
    .Output_last_32(output_last_32));
  b_32Mx64 b_32mx64_14 (
    .Input(Input[4:0]), .Select(_14), .Load(Load), .Output_first_32(Output_first_32),
    .Output_last_32(output_last_32));
  b_32Mx64 b_32mx64_15 (
    .Input(Input[4:0]), .Select(_15), .Load(Load), .Output_first_32(Output_first_32),
    .Output_last_32(output_last_32));
  b_32Mx64 b_32mx64_16 (
    .Input(Input[4:0]), .Select(_16), .Load(Load), .Output_first_32(Output_first_32),
    .Output_last_32(output_last_32));
  b_32Mx64 b_32mx64_17 (
    .Input(Input[4:0]), .Select(_17), .Load(Load), .Output_first_32(Output_first_32),
    .Output_last_32(output_last_32));
  b_32Mx64 b_32mx64_18 (
    .Input(Input[4:0]), .Select(_18), .Load(Load), .Output_first_32(Output_first_32),
    .Output_last_32(output_last_32));
  b_32Mx64 b_32mx64_19 (
    .Input(Input[4:0]), .Select(_19), .Load(Load), .Output_first_32(Output_first_32),
    .Output_last_32(output_last_32));
  b_32Mx64 b_32mx64_20 (
    .Input(Input[4:0]), .Select(_20), .Load(Load), .Output_first_32(Output_first_32),
    .Output_last_32(output_last_32));
  b_32Mx64 b_32mx64_21 (
    .Input(Input[4:0]), .Select(_21), .Load(Load), .Output_first_32(Output_first_32),
    .Output_last_32(output_last_32));
  b_32Mx64 b_32mx64_22 (
    .Input(Input[4:0]), .Select(_22), .Load(Load), .Output_first_32(Output_first_32),
    .Output_last_32(output_last_32));
  b_32Mx64 b_32mx64_23 (
    .Input(Input[4:0]), .Select(_23), .Load(Load), .Output_first_32(Output_first_32),
    .Output_last_32(output_last_32));
  b_32Mx64 b_32mx64_24 (
    .Input(Input[4:0]), .Select(_24), .Load(Load), .Output_first_32(Output_first_32),
    .Output_last_32(output_last_32));
  b_32Mx64 b_32mx64_25 (
    .Input(Input[4:0]), .Select(_25), .Load(Load), .Output_first_32(Output_first_32),
    .Output_last_32(output_last_32));
  b_32Mx64 b_32mx64_26 (
    .Input(Input[4:0]), .Select(_26), .Load(Load), .Output_first_32(Output_first_32),
    .Output_last_32(output_last_32));
  b_32Mx64 b_32mx64_27 (
    .Input(Input[4:0]), .Select(_27), .Load(Load), .Output_first_32(Output_first_32),
    .Output_last_32(output_last_32));
  b_32Mx64 b_32mx64_28 (
    .Input(Input[4:0]), .Select(_28), .Load(Load), .Output_first_32(Output_first_32),
    .Output_last_32(output_last_32));
  b_32Mx64 b_32mx64_29 (
    .Input(Input[4:0]), .Select(_29), .Load(Load), .Output_first_32(Output_first_32),
    .Output_last_32(output_last_32));
  b_32Mx64 b_32mx64_30 (
    .Input(Input[4:0]), .Select(_30), .Load(Load), .Output_first_32(Output_first_32),
    .Output_last_32(output_last_32));
  b_32Mx64 b_32mx64_31 (
    .Input(Input[4:0]), .Select(_31), .Load(Load), .Output_first_32(Output_first_32),
    .Output_last_32(output_last_32));
  b_32Mx64 b_32mx64_32 (
    .Input(Input[4:0]), .Select(_32), .Load(Load), .Output_first_32(Output_first_32),
    .Output_last_32(output_last_32));

  // Other names for the same wires on the sheet: First_5bits[4:0] = Input[4:0]; Last_5bits[4:0] = Input[9:5]
endmodule

module b_2Gx64 (
  input  [10:0] Input,
  output [31:0] Output_first_32,
  output [31:0] Output_Last_32
);

  wire decoder_1_out0, decoder_1_out1;

  Decoder #(.enable("false")) decoder_1 (.out0(decoder_1_out0), .out1(decoder_1_out1), .sel(Input[10]));
  b_1Gx64 b_1gx64_1 (
    .Input(Input[9:0]), .Select(decoder_1_out0), .Load(decoder_1_out0), .output_last_32(Output_first_32),
    .Output_first_32(Output_Last_32));
  b_1Gx64 b_1gx64_2 (
    .Input(Input[9:0]), .Select(decoder_1_out1), .Load(decoder_1_out1), .output_last_32(Output_first_32),
    .Output_first_32(Output_Last_32));
endmodule
