// Logisim project bcdu9komplement.circ as structural Verilog: 1 circuit, main circuit main
module main (
  input  A,
  input  B,
  input  C,
  input  D,
  output out_5,
  output out_6,
  output out_7,
  output out_8
);

  wire and_1_out, and_2_out, not_3_out;

  not not_1 (out_6, B);
  not not_2 (out_8, D);
  not not_3 (not_3_out, A);
  not not_4 (out_7, C);
  and and_1 (and_1_out, B, D);
  and and_2 (and_2_out, B, C);
  or or_1 (out_5, not_3_out, and_1_out, and_2_out);
endmodule
