// Logisim project citsit.circ as structural Verilog
// 1bit komp.
module _1bit_comp (
  input  A,
  input  B,
  input  in_3,
  input  in_4,
  input  in_5,
  output out,
  output out_2,
  output out_3
);

  wire A_prime_B_out, AB_prime_out, and_1_out, and_2_out, not_1_out, not_2_out, xnor_1_out;

  not not_1 (not_1_out, A);
  and A_prime_B (A_prime_B_out, not_1_out, B);
  and AB_prime (AB_prime_out, A, not_2_out);
  not not_2 (not_2_out, B);
  xnor xnor_1 (xnor_1_out, A, B);
  and and_1 (and_1_out, A_prime_B_out, in_3);
  and and_2 (and_2_out, AB_prime_out, in_3);
  and and_3 (out_3, xnor_1_out, in_3);
  or or_1 (out, and_1_out, in_4);
  or or_2 (out_2, and_2_out, in_5);

  // Notes on the sheet:
  //   <out=<in + =in.a'.b
  //   >out=>in + =in.a.b'
endmodule

module _4bit_comp (
  input  [3:0] A,
  input  [3:0] B,
  output out_3,
  output out_4,
  output out_5
);

  wire n1bit_comp_1_out, n1bit_comp_1_out_2, n1bit_comp_1_out_3, n1bit_comp_2_out, n1bit_comp_2_out_2,
       n1bit_comp_2_out_3, n1bit_comp_3_out, n1bit_comp_3_out_2, n1bit_comp_3_out_3;

  _1bit_comp u_1bit_comp_1 (
    .A(A[3]), .B(B[3]), .out(n1bit_comp_1_out), .out_2(n1bit_comp_1_out_2), .out_3(n1bit_comp_1_out_3),
    .in_3(1'b1), .in_4(1'b0), .in_5(1'b0));
  _1bit_comp u_1bit_comp_2 (
    .A(A[2]), .B(B[2]), .out(n1bit_comp_2_out), .out_2(n1bit_comp_2_out_2), .out_3(n1bit_comp_2_out_3),
    .in_3(n1bit_comp_1_out_3), .in_4(n1bit_comp_1_out), .in_5(n1bit_comp_1_out_2));
  _1bit_comp u_1bit_comp_3 (
    .A(A[1]), .B(B[1]), .out(n1bit_comp_3_out), .out_2(n1bit_comp_3_out_2), .out_3(n1bit_comp_3_out_3),
    .in_3(n1bit_comp_2_out_3), .in_4(n1bit_comp_2_out), .in_5(n1bit_comp_2_out_2));
  _1bit_comp u_1bit_comp_4 (
    .A(A[0]), .B(B[0]), .out(out_4), .out_2(out_5), .out_3(out_3), .in_3(n1bit_comp_3_out_3),
    .in_4(n1bit_comp_3_out), .in_5(n1bit_comp_3_out_2));
endmodule

module _1bit_comp_4x1mux (
  input  in_1,
  input  in_2,
  input  in_3,
  input  A,
  input  B,
  output out_6,
  output out_7,
  output out_8
);

  wire or_1_out, or_2_out;

  or or_1 (or_1_out, in_1, in_3);
  or or_2 (or_2_out, in_2, in_3);
  Multiplexer #(.select(2), .enable("false")) multiplexer_1 (
    .in0(in_1), .in1(or_1_out), .in2(in_1), .in3(in_1), .out(out_6), .sel({A, B}));
  Multiplexer #(.select(2), .enable("false")) multiplexer_2 (
    .in0(in_2), .in1(in_2), .in2(or_2_out), .in3(in_2), .out(out_7), .sel({A, B}));
  Multiplexer #(.select(2), .enable("false")) multiplexer_3 (
    .in0(in_3), .in1(1'b0), .in2(1'b0), .in3(in_3), .out(out_8), .sel({A, B}));
endmodule

module _1bit_comp_simpler (
  input  A,
  input  B,
  input  in_3,
  input  in_4,
  input  in_5,
  output out,
  output out_2,
  output out_3
);

  wire A_prime_B_out, AB_prime_out, and_1_out, and_2_out, not_1_out, not_2_out;

  not not_1 (not_1_out, A);
  and A_prime_B (A_prime_B_out, not_1_out, B);
  and AB_prime (AB_prime_out, A, not_2_out);
  not not_2 (not_2_out, B);
  and and_1 (and_1_out, A_prime_B_out, in_3);
  and and_2 (and_2_out, AB_prime_out, in_3);
  or or_1 (out, and_1_out, in_4);
  or or_2 (out_2, and_2_out, in_5);
  nor nor_1 (out_3, out_2, out);

  // Notes on the sheet:
  //   <out=<in + =in.a'.b
  //   >out=>in + =in.a.b'
  //   =out := <out' . >out' := (<out + >out)'
endmodule

module _1bit_comp_8x1mux (
  input  in_1,
  input  in_2,
  input  in_3,
  input  A,
  input  B,
  output out_6,
  output out_7,
  output out_8
);

  Multiplexer #(.select(3), .enable("false")) multiplexer_1 (
    .in0(1'b0), .in1(1'b1), .in2(in_3), .in3(1'b1), .in4(1'b0), .in5(1'b1), .in6(1'b0), .in7(1'b1),
    .out(out_6), .sel({A, B, in_1}));
  Multiplexer #(.select(3), .enable("false")) multiplexer_2 (
    .in0(1'b0), .in1(1'b1), .in2(1'b0), .in3(1'b1), .in4(in_3), .in5(1'b1), .in6(1'b0), .in7(1'b1),
    .out(out_7), .sel({A, B, in_2}));
  Multiplexer #(.select(3), .enable("false")) multiplexer_3 (
    .in0(1'b0), .in1(1'b1), .in2(1'b0), .in3(1'b0), .in4(1'b0), .in5(1'b0), .in6(1'b0), .in7(1'b1),
    .out(out_8), .sel({A, B, in_3}));
endmodule

module decoder_example (
  input  [3:0] Sensor
);

  wire decoder_1_out0, decoder_1_out12, decoder_1_out13, decoder_1_out14, decoder_1_out15;

  Decoder #(.select(4), .enable("false")) decoder_1 (
    .out0(decoder_1_out0), .out12(decoder_1_out12), .out13(decoder_1_out13), .out14(decoder_1_out14),
    .out15(decoder_1_out15), .sel(Sensor));  // open: out1, out2, out3, out4, out5, out6, out7, out8, out9, out10, out11
  LED led_1 (.in(decoder_1_out0));
  LED led_2 (.in(decoder_1_out12));
  LED led_3 (.in(decoder_1_out13));
  LED led_4 (.in(decoder_1_out14));
  LED led_5 (.in(decoder_1_out15));
endmodule

module ROM_example (
  input  [2:0] Adresa,
  output [3:0] Podatak
);

  wire decoder_1_out0, decoder_1_out1, decoder_1_out2, decoder_1_out3, decoder_1_out4, decoder_1_out5,
       decoder_1_out6, decoder_1_out7;

  Decoder #(.select(3), .enable("false")) decoder_1 (
    .out0(decoder_1_out0), .out1(decoder_1_out1), .out2(decoder_1_out2), .out3(decoder_1_out3),
    .out4(decoder_1_out4), .out5(decoder_1_out5), .out6(decoder_1_out6), .out7(decoder_1_out7), .sel(Adresa));
  or or_1 (Podatak[3], decoder_1_out0, decoder_1_out1, decoder_1_out5);
  or or_2 (Podatak[2], decoder_1_out3, decoder_1_out7);
  or or_3 (Podatak[1], decoder_1_out1, decoder_1_out2, decoder_1_out4, decoder_1_out6, decoder_1_out7);
  or or_4 (Podatak[0], decoder_1_out0, decoder_1_out1, decoder_1_out3, decoder_1_out4, decoder_1_out7);

  // Notes on the sheet:
  //   9, 11, 2, 5, 3, 8, 2, 7
endmodule

module _4bit_barrel_shifter (
  input  [3:0] in_1,
  input  [3:0] in_2,
  input  R,
  input  L,
  output [3:0] out_5,
  output [3:0] out_6
);

  Multiplexer #(.enable("false")) multiplexer_1 (.in0(in_1[0]), .in1(in_1[1]), .out(out_5[0]), .sel(R));
  Multiplexer #(.enable("false")) multiplexer_2 (.in0(in_1[1]), .in1(in_1[2]), .out(out_5[1]), .sel(R));
  Multiplexer #(.enable("false")) multiplexer_3 (.in0(in_1[2]), .in1(in_1[3]), .out(out_5[2]), .sel(R));
  Multiplexer #(.enable("false")) multiplexer_4 (.in0(in_1[3]), .in1(in_1[0]), .out(out_5[3]), .sel(R));
  Multiplexer #(.enable("false")) multiplexer_5 (.in0(in_2[0]), .in1(in_2[3]), .out(out_6[0]), .sel(L));
  Multiplexer #(.enable("false")) multiplexer_6 (.in0(in_2[1]), .in1(in_2[0]), .out(out_6[1]), .sel(L));
  Multiplexer #(.enable("false")) multiplexer_7 (.in0(in_2[2]), .in1(in_2[1]), .out(out_6[2]), .sel(L));
  Multiplexer #(.enable("false")) multiplexer_8 (.in0(in_2[3]), .in1(in_2[2]), .out(out_6[3]), .sel(L));
endmodule

module bit_barrel_shifter_full (
  input  [3:0] in_1,
  input  [1:0] R,
  output [3:0] out_3
);

  wire multiplexer_1_out, multiplexer_2_out, multiplexer_3_out, multiplexer_4_out;

  Multiplexer #(.enable("false")) multiplexer_1 (.in0(in_1[0]), .in1(in_1[2]), .out(multiplexer_1_out), .sel(R[1]));
  Multiplexer #(.enable("false")) multiplexer_2 (.in0(in_1[1]), .in1(in_1[3]), .out(multiplexer_2_out), .sel(R[1]));
  Multiplexer #(.enable("false")) multiplexer_3 (.in0(in_1[2]), .in1(in_1[0]), .out(multiplexer_3_out), .sel(R[1]));
  Multiplexer #(.enable("false")) multiplexer_4 (.in0(in_1[3]), .in1(in_1[1]), .out(multiplexer_4_out), .sel(R[1]));
  Multiplexer #(.enable("false")) multiplexer_5 (
    .in0(multiplexer_1_out), .in1(multiplexer_2_out), .out(out_3[0]), .sel(R[0]));
  Multiplexer #(.enable("false")) multiplexer_6 (
    .in0(multiplexer_2_out), .in1(multiplexer_3_out), .out(out_3[1]), .sel(R[0]));
  Multiplexer #(.enable("false")) multiplexer_7 (
    .in0(multiplexer_3_out), .in1(multiplexer_4_out), .out(out_3[2]), .sel(R[0]));
  Multiplexer #(.enable("false")) multiplexer_8 (
    .in0(multiplexer_4_out), .in1(multiplexer_1_out), .out(out_3[3]), .sel(R[0]));
endmodule

module Hexadec_to_7segment (
  input  [3:0] in_1
);

  wire decoder_1_out0, decoder_1_out1, decoder_1_out2, decoder_1_out3, decoder_1_out4, decoder_1_out5,
       decoder_1_out6, decoder_1_out7, decoder_1_out8, decoder_1_out9, decoder_1_out10, decoder_1_out11,
       decoder_1_out12, decoder_1_out13, decoder_1_out14, decoder_1_out15, or_1_out, or_2_out, or_3_out,
       or_4_out, or_5_out, or_6_out, or_7_out;

  Decoder #(.select(4), .enable("false")) decoder_1 (
    .out0(decoder_1_out0), .out1(decoder_1_out1), .out2(decoder_1_out2), .out3(decoder_1_out3),
    .out4(decoder_1_out4), .out5(decoder_1_out5), .out6(decoder_1_out6), .out7(decoder_1_out7),
    .out8(decoder_1_out8), .out9(decoder_1_out9), .out10(decoder_1_out10), .out11(decoder_1_out11),
    .out12(decoder_1_out12), .out13(decoder_1_out13), .out14(decoder_1_out14), .out15(decoder_1_out15),
    .sel(in_1));
  _7_Segment_Display u_7_segment_display_1 (
    .g(or_7_out), .f(or_6_out), .a(or_1_out), .b(or_2_out), .e(or_5_out), .d(or_4_out), .c(or_3_out));  // open: dp
  or or_1 (or_1_out, decoder_1_out0, decoder_1_out2, decoder_1_out3, decoder_1_out14, decoder_1_out5, decoder_1_out6, decoder_1_out7, decoder_1_out8, decoder_1_out9, decoder_1_out10, decoder_1_out12, decoder_1_out15);
  or or_2 (or_2_out, decoder_1_out0, decoder_1_out1, decoder_1_out2, decoder_1_out3, decoder_1_out4, decoder_1_out7, decoder_1_out8, decoder_1_out9, decoder_1_out10, decoder_1_out13);
  or or_3 (or_3_out, decoder_1_out0, decoder_1_out1, decoder_1_out3, decoder_1_out4, decoder_1_out5, decoder_1_out6, decoder_1_out7, decoder_1_out8, decoder_1_out9, decoder_1_out10, decoder_1_out11, decoder_1_out13);
  or or_4 (or_4_out, decoder_1_out0, decoder_1_out2, decoder_1_out3, decoder_1_out5, decoder_1_out6, decoder_1_out8, decoder_1_out9, decoder_1_out11, decoder_1_out12, decoder_1_out13, decoder_1_out14);
  or or_5 (or_5_out, decoder_1_out0, decoder_1_out10, decoder_1_out2, decoder_1_out6, decoder_1_out8, decoder_1_out11, decoder_1_out12, decoder_1_out13, decoder_1_out14, decoder_1_out15);
  or or_6 (or_6_out, decoder_1_out0, decoder_1_out4, decoder_1_out5, decoder_1_out6, decoder_1_out8, decoder_1_out9, decoder_1_out10, decoder_1_out11, decoder_1_out12, decoder_1_out14, decoder_1_out15);
  or or_7 (or_7_out, decoder_1_out2, decoder_1_out3, decoder_1_out4, decoder_1_out5, decoder_1_out6, decoder_1_out8, decoder_1_out9, decoder_1_out10, decoder_1_out11, decoder_1_out13, decoder_1_out14, decoder_1_out15);
endmodule

module BCD_to_9_komplement (
  input  [3:0] in_1,
  output [6:0] out_2
);

  wire decoder_1_out0, decoder_1_out1, decoder_1_out2, decoder_1_out3, decoder_1_out4, decoder_1_out5,
       decoder_1_out6, decoder_1_out7, decoder_1_out8, decoder_1_out9, decoder_1_out10, decoder_1_out11,
       decoder_1_out12, decoder_1_out13, decoder_1_out14, decoder_1_out15;

  Decoder #(.select(4), .enable("false")) decoder_1 (
    .out0(decoder_1_out0), .out1(decoder_1_out1), .out2(decoder_1_out2), .out3(decoder_1_out3),
    .out4(decoder_1_out4), .out5(decoder_1_out5), .out6(decoder_1_out6), .out7(decoder_1_out7),
    .out8(decoder_1_out8), .out9(decoder_1_out9), .out10(decoder_1_out10), .out11(decoder_1_out11),
    .out12(decoder_1_out12), .out13(decoder_1_out13), .out14(decoder_1_out14), .out15(decoder_1_out15),
    .sel(in_1));
  or or_1 (out_2[6], decoder_1_out10, decoder_1_out11, decoder_1_out12, decoder_1_out13, decoder_1_out14, decoder_1_out15);
  or or_2 (out_2[3], decoder_1_out0, decoder_1_out1, decoder_1_out10);
  or or_3 (out_2[2], decoder_1_out2, decoder_1_out3, decoder_1_out4, decoder_1_out5, decoder_1_out12, decoder_1_out13, decoder_1_out14, decoder_1_out11);
  or or_4 (out_2[1], decoder_1_out2, decoder_1_out3, decoder_1_out6, decoder_1_out7, decoder_1_out11, decoder_1_out12, decoder_1_out15);
  or or_5 (out_2[0], decoder_1_out0, decoder_1_out2, decoder_1_out4, decoder_1_out6, decoder_1_out8, decoder_1_out11, decoder_1_out13, decoder_1_out15);

  assign out_2[5:4] = {1'b0, out_2[6]};
endmodule

module xor_preko_muxa (
  input  in_1,
  input  in_2,
  output out_3
);

  wire not_1_out;

  not not_1 (not_1_out, in_1);
  Multiplexer #(.enable("false")) multiplexer_1 (.in0(in_1), .in1(not_1_out), .out(out_3), .sel(in_2));
endmodule

module komaprator (
  input  A,
  input  B,
  output manje,
  output vece,
  output jednako
);

  wire and_3_out, and_4_out, not_1_out, not_2_out, not_3_out, not_4_out;

  not not_1 (not_1_out, A);
  not not_2 (not_2_out, B);
  not not_3 (not_3_out, A);
  not not_4 (not_4_out, B);
  and and_1 (manje, not_1_out, B);
  and and_2 (vece, A, not_2_out);
  and and_3 (and_3_out, not_3_out, not_4_out);
  and and_4 (and_4_out, A, B);
  or or_1 (jednako, and_3_out, and_4_out);
endmodule
