// Logisim project davalja (1).circ as structural Verilog
// 1bit komp.
module _1bit_comp (
  input  A,
  input  B,
  input  in_3,
  input  in_4,
  input  in_5,
  output out,
  output out_2,
  output out_3
);

  wire A_prime_B_out, AB_prime_out, and_1_out, and_2_out, not_1_out, not_2_out, xnor_1_out;

  not not_1 (not_1_out, A);
  and A_prime_B (A_prime_B_out, not_1_out, B);
  and AB_prime (AB_prime_out, A, not_2_out);
  not not_2 (not_2_out, B);
  xnor xnor_1 (xnor_1_out, A, B);
  and and_1 (and_1_out, A_prime_B_out, in_3);
  and and_2 (and_2_out, AB_prime_out, in_3);
  and and_3 (out_3, xnor_1_out, in_3);
  or or_1 (out, and_1_out, in_4);
  or or_2 (out_2, and_2_out, in_5);

  // Notes on the sheet:
  //   <out=<in + =in.a'.b
  //   >out=>in + =in.a.b'
endmodule

module _4bit_comp (
  input  [3:0] A,
  input  [3:0] B,
  output out_3,
  output out_4,
  output out_5
);

  wire n1bit_comp_1_out, n1bit_comp_1_out_2, n1bit_comp_1_out_3, n1bit_comp_2_out, n1bit_comp_2_out_2,
       n1bit_comp_2_out_3, n1bit_comp_3_out, n1bit_comp_3_out_2, n1bit_comp_3_out_3;

  _1bit_comp u_1bit_comp_1 (
    .A(A[3]), .B(B[3]), .out(n1bit_comp_1_out), .out_2(n1bit_comp_1_out_2), .out_3(n1bit_comp_1_out_3),
    .in_3(1'b1), .in_4(1'b0), .in_5(1'b0));
  _1bit_comp u_1bit_comp_2 (
    .A(A[2]), .B(B[2]), .out(n1bit_comp_2_out), .out_2(n1bit_comp_2_out_2), .out_3(n1bit_comp_2_out_3),
    .in_3(n1bit_comp_1_out_3), .in_4(n1bit_comp_1_out), .in_5(n1bit_comp_1_out_2));
  _1bit_comp u_1bit_comp_3 (
    .A(A[1]), .B(B[1]), .out(n1bit_comp_3_out), .out_2(n1bit_comp_3_out_2), .out_3(n1bit_comp_3_out_3),
    .in_3(n1bit_comp_2_out_3), .in_4(n1bit_comp_2_out), .in_5(n1bit_comp_2_out_2));
  _1bit_comp u_1bit_comp_4 (
    .A(A[0]), .B(B[0]), .out(out_4), .out_2(out_5), .out_3(out_3), .in_3(n1bit_comp_3_out_3),
    .in_4(n1bit_comp_3_out), .in_5(n1bit_comp_3_out_2));
endmodule

module _1bit_comp_4x1mux (
  input  in_1,
  input  in_2,
  input  in_3,
  input  A,
  input  B,
  output out_6,
  output out_7,
  output out_8
);

  wire or_1_out, or_2_out;

  or or_1 (or_1_out, in_1, in_3);
  or or_2 (or_2_out, in_2, in_3);
  Multiplexer #(.select(2), .enable("false")) multiplexer_1 (
    .in0(in_1), .in1(or_1_out), .in2(in_1), .in3(in_1), .out(out_6), .sel({A, B}));
  Multiplexer #(.select(2), .enable("false")) multiplexer_2 (
    .in0(in_2), .in1(in_2), .in2(or_2_out), .in3(in_2), .out(out_7), .sel({A, B}));
  Multiplexer #(.select(2), .enable("false")) multiplexer_3 (
    .in0(in_3), .in1(1'b0), .in2(1'b0), .in3(in_3), .out(out_8), .sel({A, B}));
endmodule

module _1bit_comp_simpler (
  input  A,
  input  B,
  input  in_3,
  input  in_4,
  input  in_5,
  output out,
  output out_2,
  output out_3
);

  wire A_prime_B_out, AB_prime_out, and_1_out, and_2_out, not_1_out, not_2_out;

  not not_1 (not_1_out, A);
  and A_prime_B (A_prime_B_out, not_1_out, B);
  and AB_prime (AB_prime_out, A, not_2_out);
  not not_2 (not_2_out, B);
  and and_1 (and_1_out, A_prime_B_out, in_3);
  and and_2 (and_2_out, AB_prime_out, in_3);
  or or_1 (out, and_1_out, in_4);
  or or_2 (out_2, and_2_out, in_5);
  nor nor_1 (out_3, out_2, out);

  // Notes on the sheet:
  //   <out=<in + =in.a'.b
  //   >out=>in + =in.a.b'
  //   =out := <out' . >out' := (<out + >out)'
endmodule

module _1bit_comp_8x1mux (
  input  in_1,
  input  in_2,
  input  in_3,
  input  A,
  input  B,
  output out_6,
  output out_7,
  output out_8
);

  Multiplexer #(.select(3), .enable("false")) multiplexer_1 (
    .in0(1'b0), .in1(1'b1), .in2(in_3), .in3(1'b1), .in4(1'b0), .in5(1'b1), .in6(1'b0), .in7(1'b1),
    .out(out_6), .sel({A, B, in_1}));
  Multiplexer #(.select(3), .enable("false")) multiplexer_2 (
    .in0(1'b0), .in1(1'b1), .in2(1'b0), .in3(1'b1), .in4(in_3), .in5(1'b1), .in6(1'b0), .in7(1'b1),
    .out(out_7), .sel({A, B, in_2}));
  Multiplexer #(.select(3), .enable("false")) multiplexer_3 (
    .in0(1'b0), .in1(1'b1), .in2(1'b0), .in3(1'b0), .in4(1'b0), .in5(1'b0), .in6(1'b0), .in7(1'b1),
    .out(out_8), .sel({A, B, in_3}));
endmodule

module decoder_example (
  input  [3:0] Sensor
);

  wire decoder_1_out0, decoder_1_out12, decoder_1_out13, decoder_1_out14, decoder_1_out15;

  Decoder #(.select(4), .enable("false")) decoder_1 (
    .out0(decoder_1_out0), .out12(decoder_1_out12), .out13(decoder_1_out13), .out14(decoder_1_out14),
    .out15(decoder_1_out15), .sel(Sensor));  // open: out1, out2, out3, out4, out5, out6, out7, out8, out9, out10, out11
  LED led_1 (.in(decoder_1_out0));
  LED led_2 (.in(decoder_1_out12));
  LED led_3 (.in(decoder_1_out13));
  LED led_4 (.in(decoder_1_out14));
  LED led_5 (.in(decoder_1_out15));
endmodule

module ROM_example (
  input  [2:0] Adresa,
  output [3:0] Podatak
);

  wire decoder_1_out0, decoder_1_out1, decoder_1_out2, decoder_1_out3, decoder_1_out4, decoder_1_out5,
       decoder_1_out6, decoder_1_out7;

  Decoder #(.select(3), .enable("false")) decoder_1 (
    .out0(decoder_1_out0), .out1(decoder_1_out1), .out2(decoder_1_out2), .out3(decoder_1_out3),
    .out4(decoder_1_out4), .out5(decoder_1_out5), .out6(decoder_1_out6), .out7(decoder_1_out7), .sel(Adresa));
  or or_1 (Podatak[3], decoder_1_out0, decoder_1_out1, decoder_1_out5);
  or or_2 (Podatak[2], decoder_1_out3, decoder_1_out7);
  or or_3 (Podatak[1], decoder_1_out1, decoder_1_out2, decoder_1_out4, decoder_1_out6, decoder_1_out7);
  or or_4 (Podatak[0], decoder_1_out0, decoder_1_out1, decoder_1_out3, decoder_1_out4, decoder_1_out7);

  // Notes on the sheet:
  //   9, 11, 2, 5, 3, 8, 2, 7
endmodule

module _4bit_barrel_shifter (
  input  [3:0] in_1,
  input  [3:0] in_2,
  input  R,
  input  L,
  output [3:0] out_5,
  output [3:0] out_6
);

  Multiplexer #(.enable("false")) multiplexer_1 (.in0(in_1[0]), .in1(in_1[1]), .out(out_5[0]), .sel(R));
  Multiplexer #(.enable("false")) multiplexer_2 (.in0(in_1[1]), .in1(in_1[2]), .out(out_5[1]), .sel(R));
  Multiplexer #(.enable("false")) multiplexer_3 (.in0(in_1[2]), .in1(in_1[3]), .out(out_5[2]), .sel(R));
  Multiplexer #(.enable("false")) multiplexer_4 (.in0(in_1[3]), .in1(in_1[0]), .out(out_5[3]), .sel(R));
  Multiplexer #(.enable("false")) multiplexer_5 (.in0(in_2[0]), .in1(in_2[3]), .out(out_6[0]), .sel(L));
  Multiplexer #(.enable("false")) multiplexer_6 (.in0(in_2[1]), .in1(in_2[0]), .out(out_6[1]), .sel(L));
  Multiplexer #(.enable("false")) multiplexer_7 (.in0(in_2[2]), .in1(in_2[1]), .out(out_6[2]), .sel(L));
  Multiplexer #(.enable("false")) multiplexer_8 (.in0(in_2[3]), .in1(in_2[2]), .out(out_6[3]), .sel(L));
endmodule

module bit_barrel_shifter_full (
  input  [3:0] in_1,
  input  [1:0] R,
  output [3:0] out_3
);

  wire multiplexer_1_out, multiplexer_2_out, multiplexer_3_out, multiplexer_4_out;

  Multiplexer #(.enable("false")) multiplexer_1 (.in0(in_1[0]), .in1(in_1[2]), .out(multiplexer_1_out), .sel(R[1]));
  Multiplexer #(.enable("false")) multiplexer_2 (.in0(in_1[1]), .in1(in_1[3]), .out(multiplexer_2_out), .sel(R[1]));
  Multiplexer #(.enable("false")) multiplexer_3 (.in0(in_1[2]), .in1(in_1[0]), .out(multiplexer_3_out), .sel(R[1]));
  Multiplexer #(.enable("false")) multiplexer_4 (.in0(in_1[3]), .in1(in_1[1]), .out(multiplexer_4_out), .sel(R[1]));
  Multiplexer #(.enable("false")) multiplexer_5 (
    .in0(multiplexer_1_out), .in1(multiplexer_2_out), .out(out_3[0]), .sel(R[0]));
  Multiplexer #(.enable("false")) multiplexer_6 (
    .in0(multiplexer_2_out), .in1(multiplexer_3_out), .out(out_3[1]), .sel(R[0]));
  Multiplexer #(.enable("false")) multiplexer_7 (
    .in0(multiplexer_3_out), .in1(multiplexer_4_out), .out(out_3[2]), .sel(R[0]));
  Multiplexer #(.enable("false")) multiplexer_8 (
    .in0(multiplexer_4_out), .in1(multiplexer_1_out), .out(out_3[3]), .sel(R[0]));
endmodule

module Hexadec_to_7segment (
  input  [3:0] in_1
);

  wire decoder_1_out0, decoder_1_out1, decoder_1_out2, decoder_1_out3, decoder_1_out4, decoder_1_out5,
       decoder_1_out6, decoder_1_out7, decoder_1_out8, decoder_1_out9, decoder_1_out10, decoder_1_out11,
       decoder_1_out12, decoder_1_out13, decoder_1_out14, decoder_1_out15, or_1_out, or_2_out, or_3_out,
       or_4_out, or_5_out, or_6_out, or_7_out;

  Decoder #(.select(4), .enable("false")) decoder_1 (
    .out0(decoder_1_out0), .out1(decoder_1_out1), .out2(decoder_1_out2), .out3(decoder_1_out3),
    .out4(decoder_1_out4), .out5(decoder_1_out5), .out6(decoder_1_out6), .out7(decoder_1_out7),
    .out8(decoder_1_out8), .out9(decoder_1_out9), .out10(decoder_1_out10), .out11(decoder_1_out11),
    .out12(decoder_1_out12), .out13(decoder_1_out13), .out14(decoder_1_out14), .out15(decoder_1_out15),
    .sel(in_1));
  _7_Segment_Display u_7_segment_display_1 (
    .g(or_7_out), .f(or_6_out), .a(or_1_out), .b(or_2_out), .e(or_5_out), .d(or_4_out), .c(or_3_out));  // open: dp
  or or_1 (or_1_out, decoder_1_out0, decoder_1_out2, decoder_1_out3, decoder_1_out14, decoder_1_out5, decoder_1_out6, decoder_1_out7, decoder_1_out8, decoder_1_out9, decoder_1_out10, decoder_1_out12, decoder_1_out15);
  or or_2 (or_2_out, decoder_1_out0, decoder_1_out1, decoder_1_out2, decoder_1_out3, decoder_1_out4, decoder_1_out7, decoder_1_out8, decoder_1_out9, decoder_1_out10, decoder_1_out13);
  or or_3 (or_3_out, decoder_1_out0, decoder_1_out1, decoder_1_out3, decoder_1_out4, decoder_1_out5, decoder_1_out6, decoder_1_out7, decoder_1_out8, decoder_1_out9, decoder_1_out10, decoder_1_out11, decoder_1_out13);
  or or_4 (or_4_out, decoder_1_out0, decoder_1_out2, decoder_1_out3, decoder_1_out5, decoder_1_out6, decoder_1_out8, decoder_1_out9, decoder_1_out11, decoder_1_out12, decoder_1_out13, decoder_1_out14);
  or or_5 (or_5_out, decoder_1_out0, decoder_1_out10, decoder_1_out2, decoder_1_out6, decoder_1_out8, decoder_1_out11, decoder_1_out12, decoder_1_out13, decoder_1_out14, decoder_1_out15);
  or or_6 (or_6_out, decoder_1_out0, decoder_1_out4, decoder_1_out5, decoder_1_out6, decoder_1_out8, decoder_1_out9, decoder_1_out10, decoder_1_out11, decoder_1_out12, decoder_1_out14, decoder_1_out15);
  or or_7 (or_7_out, decoder_1_out2, decoder_1_out3, decoder_1_out4, decoder_1_out5, decoder_1_out6, decoder_1_out8, decoder_1_out9, decoder_1_out10, decoder_1_out11, decoder_1_out13, decoder_1_out14, decoder_1_out15);
endmodule

module BCD_to_9_komplement (
  input  [3:0] in_1,
  input  in_2,
  output [6:0] out_3
);

  wire decoder_1_out0, decoder_1_out1, decoder_1_out2, decoder_1_out3, decoder_1_out4, decoder_1_out5,
       decoder_1_out6, decoder_1_out7, decoder_1_out8, decoder_1_out9, decoder_1_out10, decoder_1_out11,
       decoder_1_out12, decoder_1_out13, decoder_1_out14, decoder_1_out15;

  Decoder #(.select(4), .enable("false")) decoder_1 (
    .out0(decoder_1_out0), .out1(decoder_1_out1), .out2(decoder_1_out2), .out3(decoder_1_out3),
    .out4(decoder_1_out4), .out5(decoder_1_out5), .out6(decoder_1_out6), .out7(decoder_1_out7),
    .out8(decoder_1_out8), .out9(decoder_1_out9), .out10(decoder_1_out10), .out11(decoder_1_out11),
    .out12(decoder_1_out12), .out13(decoder_1_out13), .out14(decoder_1_out14), .out15(decoder_1_out15),
    .sel(in_1));
  or or_1 (out_3[6], decoder_1_out10, decoder_1_out11, decoder_1_out12, decoder_1_out13, decoder_1_out14, decoder_1_out15);
  or or_2 (out_3[3], decoder_1_out0, decoder_1_out1, decoder_1_out10);
  or or_3 (out_3[2], decoder_1_out2, decoder_1_out3, decoder_1_out4, decoder_1_out5, decoder_1_out12, decoder_1_out13, decoder_1_out14, decoder_1_out11);
  or or_4 (out_3[1], decoder_1_out2, decoder_1_out3, decoder_1_out6, decoder_1_out7, decoder_1_out11, decoder_1_out12, decoder_1_out15);
  or or_5 (out_3[0], decoder_1_out0, decoder_1_out2, decoder_1_out4, decoder_1_out6, decoder_1_out8, decoder_1_out11, decoder_1_out13, decoder_1_out15);

  assign out_3[5:4] = {in_2, out_3[6]};
endmodule

module xor_preko_muxa (
  input  in_1,
  input  in_2,
  output out_3
);

  wire not_1_out;

  not not_1 (not_1_out, in_1);
  Multiplexer #(.enable("false")) multiplexer_1 (.in0(in_1), .in1(not_1_out), .out(out_3), .sel(in_2));
endmodule

module _2kk_vrijednost (
  input  A,
  input  B,
  input  C,
  input  D,
  output X,
  output Y,
  output W,
  output Z
);

  wire and_1_out, and_2_out, and_3_out, and_4_out, and_5_out, and_6_out, and_7_out, and_8_out, and_9_out,
       and_10_out, not_1_out, not_2_out, not_3_out, not_4_out, not_5_out, not_6_out, not_7_out, not_8_out;

  and and_1 (and_1_out, A, D);
  and and_2 (and_2_out, A, C);
  and and_3 (and_3_out, A, B);
  not not_1 (not_1_out, A);
  not not_2 (not_2_out, C);
  not not_3 (not_3_out, D);
  not not_4 (not_4_out, B);
  not not_5 (not_5_out, B);
  not not_6 (not_6_out, A);
  not not_7 (not_7_out, D);
  not not_8 (not_8_out, C);
  or or_1 (X, and_1_out, and_2_out, and_3_out);
  and and_4 (and_4_out, not_1_out, B);
  and and_5 (and_5_out, B, not_2_out, not_3_out);
  and and_6 (and_6_out, A, not_4_out, D);
  and and_7 (and_7_out, A, not_5_out, C);
  and and_8 (and_8_out, not_6_out, C);
  and and_9 (and_9_out, C, not_7_out);
  and and_10 (and_10_out, A, not_8_out, D);
  or or_2 (Y, and_4_out, and_5_out, and_6_out, and_7_out);
  or or_3 (W, and_8_out, and_9_out, and_10_out);

  assign Z = D;
endmodule

// 1bit sabirac
module FA_1bit (
  input  A,
  input  B,
  input  C_in,
  output S,
  output C_out
);

  wire and_1_out, not_1_out, or_1_out, xor_1_out;

  xor xor_1 (xor_1_out, A, B);
  and and_1 (and_1_out, A, B);
  or or_1 (or_1_out, A, B);
  Multiplexer #(.enable("false")) multiplexer_1 (.in0(xor_1_out), .in1(not_1_out), .out(S), .sel(C_in));
  not not_1 (not_1_out, xor_1_out);
  Multiplexer #(.enable("false")) multiplexer_2 (.in0(and_1_out), .in1(or_1_out), .out(C_out), .sel(C_in));
endmodule

module FA_1bit_4x1Mux (
  input  C_in,
  input  A,
  input  B,
  output S,
  output C_out
);

  wire not_1_out;

  not not_1 (not_1_out, C_in);
  Multiplexer #(.select(2), .enable("false")) multiplexer_1 (
    .in0(C_in), .in1(not_1_out), .in2(not_1_out), .in3(C_in), .out(S), .sel({B, A}));
  Multiplexer #(.select(2), .enable("false")) multiplexer_2 (
    .in0(1'b0), .in1(C_in), .in2(C_in), .in3(1'b1), .out(C_out), .sel({B, A}));
endmodule

module FA_1bit_elemComp (
  input  A,
  input  B,
  input  C_in,
  output S,
  output C_out
);

  wire and_1_out, and_2_out, and_3_out, xor_1_out;

  xor xor_1 (xor_1_out, A, B);
  and and_1 (and_1_out, A, B);
  and and_2 (and_2_out, A, C_in);
  and and_3 (and_3_out, B, C_in);
  xor xor_2 (S, xor_1_out, C_in);
  or or_1 (C_out, and_1_out, and_2_out, and_3_out);
endmodule

module FA_1bit_8x1Mux (
  input  A,
  input  B,
  input  C_in,
  output S,
  output C_out
);

  Multiplexer #(.select(3), .enable("false")) multiplexer_1 (
    .in0(1'b0), .in1(1'b1), .in2(1'b1), .in3(1'b0), .in4(1'b1), .in5(1'b0), .in6(1'b0), .in7(1'b1), .out(S),
    .sel({A, B, C_in}));
  Multiplexer #(.select(3), .enable("false")) multiplexer_2 (
    .in0(1'b0), .in1(1'b0), .in2(1'b0), .in3(1'b1), .in4(1'b0), .in5(1'b1), .in6(1'b1), .in7(1'b1),
    .out(C_out), .sel({A, B, C_in}));
endmodule

module _4bit_GrayToBinary (
  input  g0,
  input  g1,
  input  g2,
  input  g3,
  input  b4,
  output b0,
  output b1,
  output b3,
  output b4_2
);

  wire not_1_out, not_2_out, not_3_out, not_4_out;

  not not_1 (not_1_out, g0);
  not not_2 (not_2_out, g1);
  not not_3 (not_3_out, g2);
  not not_4 (not_4_out, g3);
  Multiplexer #(.enable("false")) multiplexer_1 (.in0(g0), .in1(not_1_out), .out(b0), .sel(b1));
  Multiplexer #(.enable("false")) multiplexer_2 (.in0(g1), .in1(not_2_out), .out(b1), .sel(b3));
  Multiplexer #(.enable("false")) multiplexer_3 (.in0(g2), .in1(not_3_out), .out(b3), .sel(b4_2));
  Multiplexer #(.enable("false")) multiplexer_4 (.in0(g3), .in1(not_4_out), .out(b4_2), .sel(b4));
endmodule

module _8bit_GrayToBinary (
  input  g0,
  input  g1,
  input  g2,
  input  g3,
  input  g4,
  input  g5,
  input  g6,
  input  g7,
  input  b8,
  output b0,
  output b1,
  output b2,
  output b3,
  output b4,
  output b5,
  output b6,
  output b7
);

  _4bit_GrayToBinary u_4bit_graytobinary_1 (
    .g0(g0), .g1(g1), .g2(g2), .g3(g3), .b4(b4), .b0(b0), .b1(b1), .b3(b2), .b4_2(b3));
  _4bit_GrayToBinary u_4bit_graytobinary_2 (
    .g0(g4), .g1(g5), .g2(g6), .g3(g7), .b4(b8), .b0(b4), .b1(b5), .b3(b6), .b4_2(b7));
endmodule

module zad1z2 (
  input  A,
  input  B,
  input  C,
  input  D,
  output Y1,
  output Y2
);

  wire and_1_out, and_2_out, and_3_out, and_4_out, and_5_out, and_6_out, and_7_out, and_8_out, and_9_out,
       and_10_out, and_11_out, and_12_out, and_13_out, and_14_out, not_1_out, not_2_out, not_3_out, not_4_out;

  not not_1 (not_1_out, A);
  not not_2 (not_2_out, B);
  not not_3 (not_3_out, C);
  not not_4 (not_4_out, D);
  and and_1 (and_1_out, not_1_out, not_2_out, not_3_out, not_4_out);
  and and_2 (and_2_out, not_1_out, B, not_3_out, not_4_out);
  and and_3 (and_3_out, not_1_out, not_2_out, C, not_4_out);
  and and_4 (and_4_out, not_1_out, not_2_out, not_3_out, not_4_out);
  and and_5 (and_5_out, not_1_out, B, C, not_4_out);
  and and_6 (and_6_out, not_1_out, not_2_out, C, D);
  and and_7 (and_7_out, A, not_2_out, not_3_out, not_4_out);
  and and_8 (and_8_out, not_1_out, B, C, not_4_out);
  and and_9 (and_9_out, A, not_2_out, C, not_4_out);
  and and_10 (and_10_out, A, B, not_3_out, not_4_out);
  and and_11 (and_11_out, A, not_2_out, not_3_out, D);
  and and_12 (and_12_out, A, B, not_3_out, not_4_out);
  and and_13 (and_13_out, A, B, C, not_4_out);
  and and_14 (and_14_out, A, B, C, D);
  or or_1 (Y1, and_1_out, and_3_out, and_2_out, and_5_out, and_7_out, and_9_out, and_10_out, and_13_out);
  or or_2 (Y2, and_14_out, and_12_out, and_11_out, and_8_out, and_6_out, and_4_out);

  // Notes on the sheet:
  //   4 bitni ulaz: 
  //   A'B'C'D'
  //   A'BC'D'
  //   A'B'CD
  //   A'B'C'D'
  //   A'BCD'
  //   A'B'CD
  //   a)Funkcija Y1: Izlaz je tacan samo ako je ulaz djeljiv sa 2
  //   AB'CD'
  //   AB'C'D'
  //   AB'C'D
  //   A'BCD'
  //   b)Funkcija Y2: Izlaz je tacan samo ako je ulaz djeljiv sa 3
  //   ABC'D'
  //   ABC'D'
  //   ABCD'
  //   ABCD
endmodule

module zad1z3 (
  input  A,
  input  B,
  input  C,
  output Y
);

  wire and_1_out, not_1_out, not_2_out, not_3_out;

  not not_1 (not_1_out, A);
  not not_2 (not_2_out, B);
  not not_3 (not_3_out, C);
  and and_1 (and_1_out, not_2_out, not_3_out);
  or or_1 (Y, not_1_out, and_1_out);

  // Notes on the sheet:
  //   B'C'
  //   Funkcija koja je tacna samo ako je ulaz manji od 5
  //   A' V B'C'
endmodule

module zad1z5 (
  input  B3,
  input  B2,
  input  B1,
  input  B0,
  input  A3,
  input  A2,
  input  A1,
  input  A0,
  input  C_in,
  output S0,
  output S1,
  output S2,
  output S3,
  output C_out
);

  wire and_1_out, and_2_out, and_3_out, and_4_out, multiplexer_2_out, multiplexer_4_out, multiplexer_6_out,
       not_1_out, not_2_out, not_3_out, not_4_out, or_1_out, or_2_out, or_3_out, or_4_out, xor_1_out,
       xor_2_out, xor_3_out, xor_4_out;

  xor xor_1 (xor_1_out, A0, B0);
  and and_1 (and_1_out, A0, B0);
  or or_1 (or_1_out, A0, B0);
  xor xor_2 (xor_2_out, A1, B1);
  and and_2 (and_2_out, A1, B1);
  or or_2 (or_2_out, A1, B1);
  xor xor_3 (xor_3_out, A2, B2);
  and and_3 (and_3_out, A2, B2);
  or or_3 (or_3_out, A2, B2);
  xor xor_4 (xor_4_out, A3, B3);
  and and_4 (and_4_out, A3, B3);
  or or_4 (or_4_out, A3, B3);
  Multiplexer #(.enable("false")) multiplexer_1 (.in0(xor_1_out), .in1(not_1_out), .out(S0), .sel(C_in));
  not not_1 (not_1_out, xor_1_out);
  Multiplexer #(.enable("false")) multiplexer_2 (.in0(and_1_out), .in1(or_1_out), .out(multiplexer_2_out), .sel(C_in));
  Multiplexer #(.enable("false")) multiplexer_3 (.in0(xor_2_out), .in1(not_2_out), .out(S1), .sel(multiplexer_2_out));
  not not_2 (not_2_out, xor_2_out);
  Multiplexer #(.enable("false")) multiplexer_4 (
    .in0(and_2_out), .in1(or_2_out), .out(multiplexer_4_out), .sel(multiplexer_2_out));
  Multiplexer #(.enable("false")) multiplexer_5 (.in0(xor_3_out), .in1(not_3_out), .out(S2), .sel(multiplexer_4_out));
  not not_3 (not_3_out, xor_3_out);
  Multiplexer #(.enable("false")) multiplexer_6 (
    .in0(and_3_out), .in1(or_3_out), .out(multiplexer_6_out), .sel(multiplexer_4_out));
  Multiplexer #(.enable("false")) multiplexer_7 (.in0(xor_4_out), .in1(not_4_out), .out(S3), .sel(multiplexer_6_out));
  not not_4 (not_4_out, xor_4_out);
  Multiplexer #(.enable("false")) multiplexer_8 (.in0(and_4_out), .in1(or_4_out), .out(C_out), .sel(multiplexer_6_out));

  // Notes on the sheet:
  //   Ulaz1
  //   Ulaz2
  //   Ulaz1
  //   Ulaz2
  //   Ulaz1
  //   Ulaz2
  //   Ulaz1
  //   Ulaz2
  //   4 bitni potpuni sabirac
  //   Jednobitni sabirac pomocu mux-a
  //   Izlaz
  //   Izlaz
  //   Izlaz
  //   Izlaz
  //   Prenos
  //   Za realizaciju 4bitnog potpunog sabiraca
  //   Koristit cemo 4 jednobitna potpuna sabiraca
endmodule

module FullAdder (
  input  [7:0] in_1,
  input  [7:0] in_2,
  output [8:0] out_3
);

  wire fa_1bit_1_s, fa_1bit_2_s, fa_1bit_3_s, fa_1bit_4_s, fa_1bit_5_s, fa_1bit_6_s, fa_1bit_7_s;

  FA_1bit fa_1bit_1 (.A(in_1[0]), .B(in_2[0]), .C_in(1'b0), .S(fa_1bit_1_s), .C_out(out_3[0]));
  FA_1bit fa_1bit_2 (.A(in_1[1]), .B(in_2[1]), .C_in(fa_1bit_1_s), .S(fa_1bit_2_s), .C_out(out_3[1]));
  FA_1bit fa_1bit_3 (.A(in_1[2]), .B(in_2[2]), .C_in(fa_1bit_2_s), .S(fa_1bit_3_s), .C_out(out_3[2]));
  FA_1bit fa_1bit_4 (.A(in_1[3]), .B(in_2[3]), .C_in(fa_1bit_3_s), .S(fa_1bit_4_s), .C_out(out_3[3]));
  FA_1bit fa_1bit_5 (.A(in_1[4]), .B(in_2[4]), .C_in(fa_1bit_4_s), .S(fa_1bit_5_s), .C_out(out_3[4]));
  FA_1bit fa_1bit_6 (.A(in_1[5]), .B(in_2[5]), .C_in(fa_1bit_5_s), .S(fa_1bit_6_s), .C_out(out_3[5]));
  FA_1bit fa_1bit_7 (.A(in_1[6]), .B(in_2[6]), .C_in(fa_1bit_6_s), .S(fa_1bit_7_s), .C_out(out_3[6]));
  FA_1bit fa_1bit_8 (.A(in_1[7]), .B(in_2[7]), .C_in(fa_1bit_7_s), .S(out_3[8]), .C_out(out_3[7]));
endmodule
