// Logisim project kvadratdvobitnog.circ as structural Verilog: 1 circuit, main circuit main
module main (
  input  A,
  input  B,
  output Y3,
  output Y2,
  output Y1,
  output Y0
);

  wire not_1_out;

  not not_1 (not_1_out, B);
  and and_1 (Y3, A, B);
  and and_2 (Y2, A, not_1_out);

  assign Y0 = B;
  assign Y1 = 1'b0;
endmodule
