// Logisim project zad2.circ as structural Verilog
module _2Zadatak (
  input  a,
  input  b,
  input  c,
  input  d,
  output y1,
  output y2,
  output y3
);

  wire and_2_out, and_3_out, and_4_out, not_1_out, not_2_out, not_3_out, not_4_out, not_5_out, not_6_out,
       not_7_out, not_8_out, not_9_out, not_10_out, or_1_out;

  not not_1 (not_1_out, c);
  or or_1 (or_1_out, not_1_out, not_2_out);
  not not_2 (not_2_out, d);
  not not_3 (not_3_out, b);
  not not_4 (not_4_out, a);
  not not_5 (not_5_out, a);
  not not_6 (not_6_out, b);
  not not_7 (not_7_out, c);
  not not_8 (not_8_out, d);
  not not_9 (not_9_out, a);
  not not_10 (not_10_out, d);
  and and_1 (y1, or_1_out, not_3_out, not_4_out);
  and and_2 (and_2_out, not_5_out, not_6_out, not_7_out, not_8_out);
  or or_2 (y2, and_2_out, and_3_out, and_4_out);
  and and_3 (and_3_out, not_9_out, b, c, d);
  and and_4 (and_4_out, a, b, c, not_10_out);

  assign y3 = d;
endmodule
